// Logisim project 16_bit_mips_single_cycle_processorl_final.circ as structural Verilog: 1 circuit, main circuit main
module main (
  input  in_1,
  output [15:0] out_2,
  output [15:0] out_3,
  output out_4,
  output [1:0] out_5,
  output [3:0] out_6
);

  wire and_1_out, CLK_out, Control_Unit_p2, Control_Unit_p3, Control_Unit_p4, Control_Unit_p5,
       Control_Unit_p6, Control_Unit_p7, Control_Unit_p8, Control_Unit_p9, Control_Unit_p10,
       n16_bit_register_file_1_p8;
  wire [2:0] multiplexer_1_out;
  wire [15:0] adder_1_out, adder_2_out, bit_extender_1_out, Jump_p3, multiplexer_2_out, multiplexer_3_out,
       multiplexer_4_out, n16_bit_alu_1_p6, PC_q, ram_1_data, rom_1_data;

  Register #(.width(16)) PC (.D(multiplexer_4_out), .Q(PC_q), .clk(CLK_out), .clr(1'b0));  // open: en
  Clock CLK (.out(CLK_out));
  Adder #(.width(16)) adder_1 (.a(PC_q), .b(16'h1), .out(adder_1_out), .cin(in_1));  // open: cout
  ROM #(.addrWidth(16), .dataWidth(16)) rom_1 (.addr(PC_q), .data(rom_1_data));  // open: sel
  // Control_Unit Control_Unit: pin names not known; wires that end beside it: rom_1_data[15:13], Control_Unit_p2, Control_Unit_p3, Control_Unit_p4, Control_Unit_p5, Control_Unit_p6, Control_Unit_p7, Control_Unit_p8, Control_Unit_p9, Control_Unit_p10
  // Jump Jump: pin names not known; wires that end beside it: adder_1_out, rom_1_data, Jump_p3
  Multiplexer #(.width(3), .enable("false")) multiplexer_1 (
    .in0(rom_1_data[9:7]), .in1(rom_1_data[6:4]), .out(multiplexer_1_out), .sel(Control_Unit_p2));
  // _16_Bit_Register_File 16_bit_register_file_1: pin names not known; wires that end beside it: rom_1_data[6:4], rom_1_data[12:10], rom_1_data[9:7], multiplexer_1_out, out_2, CLK_out, Control_Unit_p3, n16_bit_register_file_1_p8, out_3
  Adder #(.width(16)) adder_2 (.a(adder_1_out), .b(bit_extender_1_out), .out(adder_2_out));  // open: cin, cout
  Multiplexer #(.width(16), .enable("false")) multiplexer_2 (
    .in0(out_3), .in1(bit_extender_1_out), .out(multiplexer_2_out), .sel(Control_Unit_p4));
  assign bit_extender_1_out = {{9{rom_1_data[6]}}, rom_1_data[6:0]};  // Bit_Extender bit_extender_1
  and and_1 (and_1_out, Control_Unit_p8, out_4);
  // ALU_Control ALU_OP: pin names not known; wires that end beside it: Control_Unit_p10, rom_1_data[3:0], {out_6[3:2], out_5}
  Multiplexer #(.width(16), .enable("false")) multiplexer_3 (
    .in0(adder_1_out), .in1(adder_2_out), .out(multiplexer_3_out), .sel(and_1_out));
  // _16_Bit_ALU 16_bit_alu_1: pin names not known; wires that end beside it: n16_bit_register_file_1_p8, multiplexer_2_out, out_6[2], out_5, out_4, n16_bit_alu_1_p6
  Multiplexer #(.width(16), .enable("false")) multiplexer_4 (
    .in0(multiplexer_3_out), .in1(Jump_p3), .out(multiplexer_4_out), .sel(Control_Unit_p9));
  Multiplexer #(.width(16), .enable("false")) multiplexer_5 (
    .in0(n16_bit_alu_1_p6), .in1(ram_1_data), .out(out_2), .sel(Control_Unit_p7));
  RAM #(.addrWidth(16), .dataWidth(16), .bus("separate")) ram_1 (
    .addr(n16_bit_alu_1_p6), .din(out_3), .data(ram_1_data), .str(Control_Unit_p6), .clk(CLK_out),
    .ld(Control_Unit_p5));  // open: sel, clr

  assign out_6[1:0] = out_5;

  // Notes on the sheet:
  //   ISA
  //   Opcode
  //   0000 ==> AND
  //   0001==>OR
  //   0010==>ADD
  //   0110==>SUB
  //   OpCode
  //   contents of rom_1 (hex, n*v repeats v):
  //   2000 2501 6082 510 8002 5082
  //   RegDst
endmodule
