// Logisim project 32_bit_single_cycle_proccessor.circ as structural Verilog: 24 circuits, main circuit SINGLE CYCLE PROCESSOR
module SINGLE_CYCLE_PROCESSOR (
  output [5:0] out_1,
  output [4:0] out_2,
  output [4:0] out_3,
  output [4:0] out_4,
  output [15:0] out_5,
  output [31:0] out_6
);

  wire alu_1_zero, beq_out, beqcontroller_1_output, beqcontroller_1_output_2, clock_1_out, control_1_alusrc,
       control_1_jump, control_1_memread, control_1_memtoreg, control_1_memwrite, control_1_refdst,
       control_1_regwrite, not_1_out, not_2_out;
  wire [1:0] control_1_aluop;
  wire [3:0] adder_1_out;
  wire [4:0] multiplexer_1_out;
  wire [5:0] alu_control_1_b_out_3;
  wire [31:0] A1, B1, bit_extender_1_out, counter_1_q, multiplexer_2_out, multiplexer_3_out,
       multiplexer_4_out, ram_2_data, registerfile_1_p1;
  wire [31:4] adder_1_out_2;

  // Probe on counter_1_q
  // Probe on multiplexer_4_out
  not not_1 (not_1_out, beqcontroller_1_output);
  Counter #(.width(32), .max('hffffffff), .ongoal("load")) counter_1 (
    .load(beqcontroller_1_output), .D(multiplexer_4_out), .count(not_1_out), .Q(counter_1_q),
    .clk(clock_1_out));  // open: carry, clr
  RAM #(.addrWidth(5), .dataWidth(32)) ram_1 (
    .addr(counter_1_q[4:0]), .data({out_1, out_2, out_3, out_4, out_5[10:0]}), .clk(clock_1_out), .ld(1'b1));  // open: sel, clr
  Adder #(.width(32)) adder_1 (.a(counter_1_q), .b(32'h1), .out({adder_1_out_2, adder_1_out}));  // open: cin, cout
  // Probe on registerfile_1_p1
  Clock clock_1 (.out(clock_1_out));
  // Probe on {out_5[0], out_5[1], out_5[2], out_5[3], out_5[4], out_5[5]}
  beqcontroller beqcontroller_1 (
    .Controller_IN(out_1), .A(B1), .B(A1), .OUTPUT(beqcontroller_1_output),
    .OUTPUT_2(beqcontroller_1_output_2));
  Multiplexer #(.width(5), .enable("false")) multiplexer_1 (
    .in0(out_3), .in1(out_4), .out(multiplexer_1_out), .sel(control_1_refdst));
  assign bit_extender_1_out = {{16{1'b0}}, {out_4, out_5[10:0]}};  // Bit_Extender bit_extender_1
  CONTROL control_1 (
    .Controller_IN(out_1), .RefDst(control_1_refdst), .MemRead(control_1_memread),
    .MemtoReg(control_1_memtoreg), .ALUOp(control_1_aluop), .MemWrite(control_1_memwrite),
    .ALUSrc(control_1_alusrc), .RegWrite(control_1_regwrite), .JUMP(control_1_jump));  // open: Branch
  and beq (beq_out, ~beqcontroller_1_output, ~beqcontroller_1_output_2, ~control_1_memwrite, control_1_regwrite);  // AND_Gate
  // RegisterFile registerfile_1: pin names not known; wires that end beside it: registerfile_1_p1, clock_1_out, beq_out, multiplexer_1_out, out_2, out_3, A1, B1
  // Probe on out_2
  // Probe on control_1_aluop
  Multiplexer #(.width(32), .enable("false")) multiplexer_2 (
    .in0(B1), .in1(bit_extender_1_out), .out(multiplexer_2_out), .sel(control_1_alusrc));
  // Probe on multiplexer_2_out
  // Probe on nothing
  // Probe on alu_control_1_b_out_3
  ALU_CONTROL alu_control_1 (
    .B_OUT_2({out_5[0], out_5[1], out_5[2], out_5[3], out_5[4], out_5[5]}), .B_OUT_3(alu_control_1_b_out_3),
    .B_OUT(control_1_aluop));
  // Probe on A1
  // Probe on multiplexer_2_out
  ALU alu_1 (
    .A(A1), .B(multiplexer_2_out), ._32_BIT_OUT_ALU(out_6), .OPCODE(alu_control_1_b_out_3), .ZERO(alu_1_zero));  // open: Overflow
  // Probe on alu_control_1_b_out_3
  // Probe on registerfile_1_p1
  Multiplexer #(.width(32), .enable("false")) multiplexer_3 (
    .in0({adder_1_out_2, adder_1_out}), .in1(bit_extender_1_out), .out(multiplexer_3_out),
    .sel(beqcontroller_1_output));
  Multiplexer #(.width(32), .enable("false")) multiplexer_4 (
    .in0(multiplexer_3_out),
    .in1({out_5[0], out_5[1], out_5[2], out_5[3], out_5[4], out_5[5], out_5[0], out_5[1], out_5[2], out_5[3], out_5[4], out_5[5], out_5[6], out_5[7], out_5[8], out_5[9], out_5[10], out_4[0], out_4[1], out_4[2], out_4[3], out_4[4], out_4[0], out_4[1], out_4[2], out_4[3], 2'b00, adder_1_out}),
    .out(multiplexer_4_out), .sel(control_1_jump));
  // Probe on ram_2_data
  RAM #(.addrWidth(5), .dataWidth(32), .bus("separate")) ram_2 (
    .addr(out_6[4:0]), .din(B1), .data(ram_2_data), .str(control_1_memwrite), .clk(clock_1_out),
    .ld(control_1_memread));  // open: sel, clr
  // Probe on registerfile_1_p1
  not not_2 (not_2_out, control_1_memtoreg);
  Multiplexer #(.width(32), .enable("false")) multiplexer_5 (
    .in0(ram_2_data), .in1(out_6), .out(registerfile_1_p1), .sel(not_2_out));

  assign out_5[15:11] = out_4;
endmodule

module ALU (
  input  [31:0] A,
  input  [31:0] B,
  input  [5:0] OPCODE,
  output ZERO,
  output [31:0] _32_BIT_OUT_ALU,
  output Overflow
);

  wire comparator_1_gt, n32_bit_fulladder_1_carry_out, n32_bit_sub_1_carry_out, not_1_out;
  wire [31:0] bit_extender_1_out, equal_1_output, n32_bit_and_1__4_bit_out_and, n32_bit_fulladder_1_sum,
       n32_bit_multiplier_1_b_out, n32_bit_number_combiner_1_o, n32_bit_or_1__4_bit_out_and,
       n32_bit_shift_left_1_sum, n32_bit_shift_right_1_sum, n32_bit_shift_right_arithmetic_1_sum,
       n32_bit_sub_1_sum, n32_bit_xor_1__4_bit_out_and, not_equal_1_output;

  _32_BIT_NUMBER_COMBINER u_32_bit_number_combiner_1 (.A(A), .B(B), .O(n32_bit_number_combiner_1_o));
  EQUAL equal_1 (.A(A), .B(B), .OUTPUT(equal_1_output));
  NOT_EQUAL not_equal_1 (.A(A), .B(B), .OUTPUT(not_equal_1_output));
  _32_BIT_SHIFT_LEFT u_32_bit_shift_left_1 (.A(A), .B(B), .Sum(n32_bit_shift_left_1_sum));
  _32_BIT_MULTIPLIER u_32_bit_multiplier_1 (.A(A), .B(B), .B_OUT(n32_bit_multiplier_1_b_out));
  _32_BIT_OR u_32_bit_or_1 (.A(A), .B(B), ._4_BIT_OUT_AND(n32_bit_or_1__4_bit_out_and));
  _32_BIT_XOR u_32_bit_xor_1 (.A(A), .B(B), ._4_BIT_OUT_AND(n32_bit_xor_1__4_bit_out_and));
  _32_BIT_AND u_32_bit_and_1 (.A(A), .B(B), ._4_BIT_OUT_AND(n32_bit_and_1__4_bit_out_and));
  Comparator #(.width(32)) comparator_1 (.a(A), .b(B), .gt(comparator_1_gt));  // open: eq, lt
  _32_BIT_SHIFT_RIGHT_ARITHMETIC u_32_bit_shift_right_arithmetic_1 (
    .A(A), .B(B), .Sum(n32_bit_shift_right_arithmetic_1_sum));
  _32_BIT_SHIFT_RIGHT u_32_bit_shift_right_1 (.A(A), .B(B), .Sum(n32_bit_shift_right_1_sum));
  _32_BIT_SUB u_32_bit_sub_1 (.A(A), .B(B), .Carry(1'b0), .Sum(n32_bit_sub_1_sum), .Carry_Out(n32_bit_sub_1_carry_out));
  _32_BIT_FULLADDER u_32_bit_fulladder_1 (
    .Carry(1'b0), .A(A), .B(B), .Sum(n32_bit_fulladder_1_sum), .Carry_Out(n32_bit_fulladder_1_carry_out));
  assign bit_extender_1_out = {{31{1'b0}}, comparator_1_gt};  // Bit_Extender bit_extender_1
  // Probe on n32_bit_fulladder_1_sum
  Multiplexer #(.select(4), .width(32), .enable("false")) multiplexer_1 (
    .in0(n32_bit_sub_1_sum), .in1(n32_bit_fulladder_1_sum), .in2(n32_bit_shift_left_1_sum),
    .in3(n32_bit_multiplier_1_b_out), .in4(n32_bit_or_1__4_bit_out_and), .in5(n32_bit_xor_1__4_bit_out_and),
    .in6(n32_bit_and_1__4_bit_out_and), .in7(bit_extender_1_out), .in8(n32_bit_shift_right_arithmetic_1_sum),
    .in9(n32_bit_shift_right_1_sum), .in10(n32_bit_number_combiner_1_o), .in11(equal_1_output),
    .in12(not_equal_1_output), .out(_32_BIT_OUT_ALU), .sel(OPCODE[3:0]));  // open: in13, in14, in15
  Multiplexer #(.select(2)) multiplexer_2 (
    .in1(n32_bit_fulladder_1_carry_out), .in3(n32_bit_sub_1_carry_out), .out(Overflow), .sel(OPCODE[1:0]),
    .en(not_1_out));  // open: in0, in2
  not not_1 (not_1_out, OPCODE[2]);
  _32_BIT_SET_LESS_THAN u_32_bit_set_less_than_1 ();  // open: A, B, out_3

  assign ZERO = 1'b0;

  // Notes on the sheet:
  //   OP CODE OPERATION
  //   OP CODE CARRY
endmodule

module PC (
  input  [31:0] PC_IN,
  input  [31:0] PC_OUT,
  input  in_3
);


  assign PC_OUT = PC_IN;
endmodule

module ALU_CONTROL (
  input  [1:0] B_OUT,
  input  [5:0] B_OUT_2,
  output [5:0] B_OUT_3
);

  wire [5:0] multiplexer_1_out;
  wire [5:4] undriven;

  Multiplexer #(.width(6), .enable("false")) multiplexer_1 (
    .in0(6'b000001), .in1({undriven, B_OUT_2[3:0]}), .out(multiplexer_1_out), .sel(B_OUT[0]));
  Multiplexer #(.width(6), .enable("false")) multiplexer_2 (
    .in0(multiplexer_1_out), .in1({undriven, B_OUT_2[3:0]}), .out(B_OUT_3), .sel(B_OUT[1]));
endmodule

module CONTROL (
  input  [5:0] Controller_IN,
  output RefDst,
  output JUMP,
  output Branch,
  output MemRead,
  output MemtoReg,
  output [1:0] ALUOp,
  output MemWrite,
  output ALUSrc,
  output RegWrite
);

  wire not_1_out, not_2_out, or_1_out;

  and and_1 (ALUOp[0], ~Controller_IN[5], ~Controller_IN[4], ~Controller_IN[3], ~Controller_IN[2], ~Controller_IN[1], ~Controller_IN[0]);  // AND_Gate
  and and_2 (MemRead, Controller_IN[5], ~Controller_IN[4], ~Controller_IN[3], ~Controller_IN[2], Controller_IN[1], Controller_IN[0]);  // AND_Gate
  and and_3 (MemWrite, Controller_IN[5], Controller_IN[4], ~Controller_IN[3], Controller_IN[2], ~Controller_IN[1], Controller_IN[0]);  // AND_Gate
  and and_4 (ALUOp[1], ~Controller_IN[5], ~Controller_IN[4], ~Controller_IN[3], Controller_IN[2], ~Controller_IN[1], ~Controller_IN[0]);  // AND_Gate
  not not_1 (not_1_out, ALUOp[0]);
  not not_2 (not_2_out, MemRead);
  or or_1 (or_1_out, not_1_out, not_2_out);
  buf and_5 (RegWrite, ~ALUOp[1]);  // AND_Gate AND_Gate
  or or_2 (ALUSrc, MemRead, ~ALUOp[0], MemWrite);  // OR_Gate

  assign Branch = ALUOp[1];
  assign JUMP = ALUOp[1];
  assign MemtoReg = MemRead;
  assign RefDst = ALUOp[0];
endmodule

module _32_BIT_SUB (
  input  Carry,
  input  [31:0] A,
  input  [31:0] B,
  output [31:0] Sum,
  output Carry_Out
);

  wire n1_bit_sub_1_carry_out, n1_bit_sub_2_carry_out, n1_bit_sub_3_carry_out, n1_bit_sub_4_carry_out,
       n1_bit_sub_5_carry_out, n1_bit_sub_6_carry_out, n1_bit_sub_7_carry_out, n1_bit_sub_8_carry_out,
       n1_bit_sub_9_carry_out, n1_bit_sub_10_carry_out, n1_bit_sub_11_carry_out, n1_bit_sub_12_carry_out,
       n1_bit_sub_13_carry_out, n1_bit_sub_14_carry_out, n1_bit_sub_15_carry_out, n1_bit_sub_16_carry_out,
       n1_bit_sub_17_carry_out, n1_bit_sub_18_carry_out, n1_bit_sub_19_carry_out, n1_bit_sub_20_carry_out,
       n1_bit_sub_21_carry_out, n1_bit_sub_22_carry_out, n1_bit_sub_23_carry_out, n1_bit_sub_24_carry_out,
       n1_bit_sub_25_carry_out, n1_bit_sub_26_carry_out, n1_bit_sub_27_carry_out, n1_bit_sub_28_carry_out,
       n1_bit_sub_29_carry_out, n1_bit_sub_30_carry_out, n1_bit_sub_31_carry_out;

  _1_BIT_SUB u_1_bit_sub_1 (.A(A[0]), .B(B[0]), .Carry(Carry), .difference(Sum[0]), .Carry_Out(n1_bit_sub_1_carry_out));
  _1_BIT_SUB u_1_bit_sub_2 (
    .A(A[1]), .B(B[1]), .Carry(n1_bit_sub_1_carry_out), .difference(Sum[1]),
    .Carry_Out(n1_bit_sub_2_carry_out));
  _1_BIT_SUB u_1_bit_sub_3 (
    .A(A[2]), .B(B[2]), .Carry(n1_bit_sub_2_carry_out), .difference(Sum[2]),
    .Carry_Out(n1_bit_sub_3_carry_out));
  _1_BIT_SUB u_1_bit_sub_4 (
    .A(A[3]), .B(B[3]), .Carry(n1_bit_sub_3_carry_out), .difference(Sum[3]),
    .Carry_Out(n1_bit_sub_4_carry_out));
  _1_BIT_SUB u_1_bit_sub_5 (
    .A(A[4]), .B(B[4]), .Carry(n1_bit_sub_4_carry_out), .difference(Sum[4]),
    .Carry_Out(n1_bit_sub_5_carry_out));
  _1_BIT_SUB u_1_bit_sub_6 (
    .A(A[5]), .B(B[5]), .Carry(n1_bit_sub_5_carry_out), .difference(Sum[5]),
    .Carry_Out(n1_bit_sub_6_carry_out));
  _1_BIT_SUB u_1_bit_sub_7 (
    .A(A[6]), .B(B[6]), .Carry(n1_bit_sub_6_carry_out), .difference(Sum[6]),
    .Carry_Out(n1_bit_sub_7_carry_out));
  _1_BIT_SUB u_1_bit_sub_8 (
    .A(A[7]), .B(B[7]), .Carry(n1_bit_sub_7_carry_out), .difference(Sum[7]),
    .Carry_Out(n1_bit_sub_8_carry_out));
  _1_BIT_SUB u_1_bit_sub_9 (
    .A(A[8]), .B(B[8]), .Carry(n1_bit_sub_8_carry_out), .difference(Sum[8]),
    .Carry_Out(n1_bit_sub_9_carry_out));
  _1_BIT_SUB u_1_bit_sub_10 (
    .A(A[9]), .B(B[9]), .Carry(n1_bit_sub_9_carry_out), .difference(Sum[9]),
    .Carry_Out(n1_bit_sub_10_carry_out));
  _1_BIT_SUB u_1_bit_sub_11 (
    .A(A[10]), .B(B[10]), .Carry(n1_bit_sub_10_carry_out), .difference(Sum[10]),
    .Carry_Out(n1_bit_sub_11_carry_out));
  _1_BIT_SUB u_1_bit_sub_12 (
    .A(A[11]), .B(B[11]), .Carry(n1_bit_sub_11_carry_out), .difference(Sum[11]),
    .Carry_Out(n1_bit_sub_12_carry_out));
  _1_BIT_SUB u_1_bit_sub_13 (
    .A(A[12]), .B(B[12]), .Carry(n1_bit_sub_12_carry_out), .difference(Sum[12]),
    .Carry_Out(n1_bit_sub_13_carry_out));
  _1_BIT_SUB u_1_bit_sub_14 (
    .A(A[13]), .B(B[13]), .Carry(n1_bit_sub_13_carry_out), .difference(Sum[13]),
    .Carry_Out(n1_bit_sub_14_carry_out));
  _1_BIT_SUB u_1_bit_sub_15 (
    .A(A[14]), .B(B[14]), .Carry(n1_bit_sub_14_carry_out), .difference(Sum[14]),
    .Carry_Out(n1_bit_sub_15_carry_out));
  _1_BIT_SUB u_1_bit_sub_16 (
    .A(A[15]), .B(B[15]), .Carry(n1_bit_sub_15_carry_out), .difference(Sum[15]),
    .Carry_Out(n1_bit_sub_16_carry_out));
  _1_BIT_SUB u_1_bit_sub_17 (
    .A(A[16]), .B(B[16]), .Carry(n1_bit_sub_16_carry_out), .difference(Sum[16]),
    .Carry_Out(n1_bit_sub_17_carry_out));
  _1_BIT_SUB u_1_bit_sub_18 (
    .A(A[17]), .B(B[17]), .Carry(n1_bit_sub_17_carry_out), .difference(Sum[17]),
    .Carry_Out(n1_bit_sub_18_carry_out));
  _1_BIT_SUB u_1_bit_sub_19 (
    .A(A[18]), .B(B[18]), .Carry(n1_bit_sub_18_carry_out), .difference(Sum[18]),
    .Carry_Out(n1_bit_sub_19_carry_out));
  _1_BIT_SUB u_1_bit_sub_20 (
    .A(A[19]), .B(B[19]), .Carry(n1_bit_sub_19_carry_out), .difference(Sum[19]),
    .Carry_Out(n1_bit_sub_20_carry_out));
  _1_BIT_SUB u_1_bit_sub_21 (
    .A(A[20]), .B(B[20]), .Carry(n1_bit_sub_20_carry_out), .difference(Sum[20]),
    .Carry_Out(n1_bit_sub_21_carry_out));
  _1_BIT_SUB u_1_bit_sub_22 (
    .A(A[21]), .B(B[21]), .Carry(n1_bit_sub_21_carry_out), .difference(Sum[21]),
    .Carry_Out(n1_bit_sub_22_carry_out));
  _1_BIT_SUB u_1_bit_sub_23 (
    .A(A[22]), .B(B[22]), .Carry(n1_bit_sub_22_carry_out), .difference(Sum[22]),
    .Carry_Out(n1_bit_sub_23_carry_out));
  _1_BIT_SUB u_1_bit_sub_24 (
    .A(A[23]), .B(B[23]), .Carry(n1_bit_sub_23_carry_out), .difference(Sum[23]),
    .Carry_Out(n1_bit_sub_24_carry_out));
  _1_BIT_SUB u_1_bit_sub_25 (
    .A(A[24]), .B(B[24]), .Carry(n1_bit_sub_24_carry_out), .difference(Sum[24]),
    .Carry_Out(n1_bit_sub_25_carry_out));
  _1_BIT_SUB u_1_bit_sub_26 (
    .A(A[25]), .B(B[25]), .Carry(n1_bit_sub_25_carry_out), .difference(Sum[25]),
    .Carry_Out(n1_bit_sub_26_carry_out));
  _1_BIT_SUB u_1_bit_sub_27 (
    .A(A[26]), .B(B[26]), .Carry(n1_bit_sub_26_carry_out), .difference(Sum[26]),
    .Carry_Out(n1_bit_sub_27_carry_out));
  _1_BIT_SUB u_1_bit_sub_28 (
    .A(A[27]), .B(B[27]), .Carry(n1_bit_sub_27_carry_out), .difference(Sum[27]),
    .Carry_Out(n1_bit_sub_28_carry_out));
  _1_BIT_SUB u_1_bit_sub_29 (
    .A(A[28]), .B(B[28]), .Carry(n1_bit_sub_28_carry_out), .difference(Sum[28]),
    .Carry_Out(n1_bit_sub_29_carry_out));
  _1_BIT_SUB u_1_bit_sub_30 (
    .A(A[29]), .B(B[29]), .Carry(n1_bit_sub_29_carry_out), .difference(Sum[29]),
    .Carry_Out(n1_bit_sub_30_carry_out));
  _1_BIT_SUB u_1_bit_sub_31 (
    .A(A[30]), .B(B[30]), .Carry(n1_bit_sub_30_carry_out), .difference(Sum[30]),
    .Carry_Out(n1_bit_sub_31_carry_out));
  _1_BIT_SUB u_1_bit_sub_32 (
    .A(A[31]), .B(B[31]), .Carry(n1_bit_sub_31_carry_out), .difference(Sum[31]), .Carry_Out(Carry_Out));

  // Other names for the same wires on the sheet: C = Carry
endmodule

module _32_BIT_FULLADDER (
  input  Carry,
  input  [31:0] A,
  input  [31:0] B,
  output [31:0] Sum,
  output Carry_Out
);

  wire n1_bit_fulladder_1_carry_out, n1_bit_fulladder_2_carry_out, n1_bit_fulladder_3_carry_out,
       n1_bit_fulladder_4_carry_out, n1_bit_fulladder_5_carry_out, n1_bit_fulladder_6_carry_out,
       n1_bit_fulladder_7_carry_out, n1_bit_fulladder_8_carry_out, n1_bit_fulladder_9_carry_out,
       n1_bit_fulladder_10_carry_out, n1_bit_fulladder_11_carry_out, n1_bit_fulladder_12_carry_out,
       n1_bit_fulladder_13_carry_out, n1_bit_fulladder_14_carry_out, n1_bit_fulladder_15_carry_out,
       n1_bit_fulladder_16_carry_out, n1_bit_fulladder_17_carry_out, n1_bit_fulladder_18_carry_out,
       n1_bit_fulladder_19_carry_out, n1_bit_fulladder_20_carry_out, n1_bit_fulladder_21_carry_out,
       n1_bit_fulladder_22_carry_out, n1_bit_fulladder_23_carry_out, n1_bit_fulladder_24_carry_out,
       n1_bit_fulladder_25_carry_out, n1_bit_fulladder_26_carry_out, n1_bit_fulladder_27_carry_out,
       n1_bit_fulladder_28_carry_out, n1_bit_fulladder_29_carry_out, n1_bit_fulladder_30_carry_out,
       n1_bit_fulladder_31_carry_out;

  _1_BIT_FULLADDER u_1_bit_fulladder_1 (
    .A(A[0]), .B(B[0]), .Carry(Carry), .Sum(Sum[0]), .Carry_Out(n1_bit_fulladder_1_carry_out));
  _1_BIT_FULLADDER u_1_bit_fulladder_2 (
    .A(A[1]), .B(B[1]), .Carry(n1_bit_fulladder_1_carry_out), .Sum(Sum[1]),
    .Carry_Out(n1_bit_fulladder_2_carry_out));
  _1_BIT_FULLADDER u_1_bit_fulladder_3 (
    .A(A[2]), .B(B[2]), .Carry(n1_bit_fulladder_2_carry_out), .Sum(Sum[2]),
    .Carry_Out(n1_bit_fulladder_3_carry_out));
  _1_BIT_FULLADDER u_1_bit_fulladder_4 (
    .A(A[3]), .B(B[3]), .Carry(n1_bit_fulladder_3_carry_out), .Sum(Sum[3]),
    .Carry_Out(n1_bit_fulladder_4_carry_out));
  _1_BIT_FULLADDER u_1_bit_fulladder_5 (
    .A(A[4]), .B(B[4]), .Carry(n1_bit_fulladder_4_carry_out), .Sum(Sum[4]),
    .Carry_Out(n1_bit_fulladder_5_carry_out));
  _1_BIT_FULLADDER u_1_bit_fulladder_6 (
    .A(A[5]), .B(B[5]), .Carry(n1_bit_fulladder_5_carry_out), .Sum(Sum[5]),
    .Carry_Out(n1_bit_fulladder_6_carry_out));
  _1_BIT_FULLADDER u_1_bit_fulladder_7 (
    .A(A[6]), .B(B[6]), .Carry(n1_bit_fulladder_6_carry_out), .Sum(Sum[6]),
    .Carry_Out(n1_bit_fulladder_7_carry_out));
  _1_BIT_FULLADDER u_1_bit_fulladder_8 (
    .A(A[7]), .B(B[7]), .Carry(n1_bit_fulladder_7_carry_out), .Sum(Sum[7]),
    .Carry_Out(n1_bit_fulladder_8_carry_out));
  _1_BIT_FULLADDER u_1_bit_fulladder_9 (
    .A(A[8]), .B(B[8]), .Carry(n1_bit_fulladder_8_carry_out), .Sum(Sum[8]),
    .Carry_Out(n1_bit_fulladder_9_carry_out));
  _1_BIT_FULLADDER u_1_bit_fulladder_10 (
    .A(A[9]), .B(B[9]), .Carry(n1_bit_fulladder_9_carry_out), .Sum(Sum[9]),
    .Carry_Out(n1_bit_fulladder_10_carry_out));
  _1_BIT_FULLADDER u_1_bit_fulladder_11 (
    .A(A[10]), .B(B[10]), .Carry(n1_bit_fulladder_10_carry_out), .Sum(Sum[10]),
    .Carry_Out(n1_bit_fulladder_11_carry_out));
  _1_BIT_FULLADDER u_1_bit_fulladder_12 (
    .A(A[11]), .B(B[11]), .Carry(n1_bit_fulladder_11_carry_out), .Sum(Sum[11]),
    .Carry_Out(n1_bit_fulladder_12_carry_out));
  _1_BIT_FULLADDER u_1_bit_fulladder_13 (
    .A(A[12]), .B(B[12]), .Carry(n1_bit_fulladder_12_carry_out), .Sum(Sum[12]),
    .Carry_Out(n1_bit_fulladder_13_carry_out));
  _1_BIT_FULLADDER u_1_bit_fulladder_14 (
    .A(A[13]), .B(B[13]), .Carry(n1_bit_fulladder_13_carry_out), .Sum(Sum[13]),
    .Carry_Out(n1_bit_fulladder_14_carry_out));
  _1_BIT_FULLADDER u_1_bit_fulladder_15 (
    .A(A[14]), .B(B[14]), .Carry(n1_bit_fulladder_14_carry_out), .Sum(Sum[14]),
    .Carry_Out(n1_bit_fulladder_15_carry_out));
  _1_BIT_FULLADDER u_1_bit_fulladder_16 (
    .A(A[15]), .B(B[15]), .Carry(n1_bit_fulladder_15_carry_out), .Sum(Sum[15]),
    .Carry_Out(n1_bit_fulladder_16_carry_out));
  _1_BIT_FULLADDER u_1_bit_fulladder_17 (
    .A(A[16]), .B(B[16]), .Carry(n1_bit_fulladder_16_carry_out), .Sum(Sum[16]),
    .Carry_Out(n1_bit_fulladder_17_carry_out));
  _1_BIT_FULLADDER u_1_bit_fulladder_18 (
    .A(A[17]), .B(B[17]), .Carry(n1_bit_fulladder_17_carry_out), .Sum(Sum[17]),
    .Carry_Out(n1_bit_fulladder_18_carry_out));
  _1_BIT_FULLADDER u_1_bit_fulladder_19 (
    .A(A[18]), .B(B[18]), .Carry(n1_bit_fulladder_18_carry_out), .Sum(Sum[18]),
    .Carry_Out(n1_bit_fulladder_19_carry_out));
  _1_BIT_FULLADDER u_1_bit_fulladder_20 (
    .A(A[19]), .B(B[19]), .Carry(n1_bit_fulladder_19_carry_out), .Sum(Sum[19]),
    .Carry_Out(n1_bit_fulladder_20_carry_out));
  _1_BIT_FULLADDER u_1_bit_fulladder_21 (
    .A(A[20]), .B(B[20]), .Carry(n1_bit_fulladder_20_carry_out), .Sum(Sum[20]),
    .Carry_Out(n1_bit_fulladder_21_carry_out));
  _1_BIT_FULLADDER u_1_bit_fulladder_22 (
    .A(A[21]), .B(B[21]), .Carry(n1_bit_fulladder_21_carry_out), .Sum(Sum[21]),
    .Carry_Out(n1_bit_fulladder_22_carry_out));
  _1_BIT_FULLADDER u_1_bit_fulladder_23 (
    .A(A[22]), .B(B[22]), .Carry(n1_bit_fulladder_22_carry_out), .Sum(Sum[22]),
    .Carry_Out(n1_bit_fulladder_23_carry_out));
  _1_BIT_FULLADDER u_1_bit_fulladder_24 (
    .A(A[23]), .B(B[23]), .Carry(n1_bit_fulladder_23_carry_out), .Sum(Sum[23]),
    .Carry_Out(n1_bit_fulladder_24_carry_out));
  _1_BIT_FULLADDER u_1_bit_fulladder_25 (
    .A(A[24]), .B(B[24]), .Carry(n1_bit_fulladder_24_carry_out), .Sum(Sum[24]),
    .Carry_Out(n1_bit_fulladder_25_carry_out));
  _1_BIT_FULLADDER u_1_bit_fulladder_26 (
    .A(A[25]), .B(B[25]), .Carry(n1_bit_fulladder_25_carry_out), .Sum(Sum[25]),
    .Carry_Out(n1_bit_fulladder_26_carry_out));
  _1_BIT_FULLADDER u_1_bit_fulladder_27 (
    .A(A[26]), .B(B[26]), .Carry(n1_bit_fulladder_26_carry_out), .Sum(Sum[26]),
    .Carry_Out(n1_bit_fulladder_27_carry_out));
  _1_BIT_FULLADDER u_1_bit_fulladder_28 (
    .A(A[27]), .B(B[27]), .Carry(n1_bit_fulladder_27_carry_out), .Sum(Sum[27]),
    .Carry_Out(n1_bit_fulladder_28_carry_out));
  _1_BIT_FULLADDER u_1_bit_fulladder_29 (
    .A(A[28]), .B(B[28]), .Carry(n1_bit_fulladder_28_carry_out), .Sum(Sum[28]),
    .Carry_Out(n1_bit_fulladder_29_carry_out));
  _1_BIT_FULLADDER u_1_bit_fulladder_30 (
    .A(A[29]), .B(B[29]), .Carry(n1_bit_fulladder_29_carry_out), .Sum(Sum[29]),
    .Carry_Out(n1_bit_fulladder_30_carry_out));
  _1_BIT_FULLADDER u_1_bit_fulladder_31 (
    .A(A[30]), .B(B[30]), .Carry(n1_bit_fulladder_30_carry_out), .Sum(Sum[30]),
    .Carry_Out(n1_bit_fulladder_31_carry_out));
  _1_BIT_FULLADDER u_1_bit_fulladder_32 (
    .A(A[31]), .B(B[31]), .Carry(n1_bit_fulladder_31_carry_out), .Sum(Sum[31]), .Carry_Out(Carry_Out));

  // Other names for the same wires on the sheet: C = Carry
endmodule

module _32_BIT_MULTIPLIER (
  input  [31:0] A,
  input  [31:0] B,
  output [31:0] B_OUT
);

  wire [31:0] bit_extender_1_out, bit_extender_2_out, bit_extender_3_out, bit_extender_4_out,
       bit_extender_5_out, bit_extender_6_out, bit_extender_7_out, bit_extender_8_out, bit_extender_9_out,
       bit_extender_10_out, bit_extender_11_out, bit_extender_12_out, bit_extender_13_out,
       bit_extender_14_out, bit_extender_15_out, bit_extender_16_out, line1, line2,
       n32_bit_and_1__4_bit_out_and, n32_bit_and_2__4_bit_out_and, n32_bit_and_3__4_bit_out_and,
       n32_bit_and_4__4_bit_out_and, n32_bit_and_5__4_bit_out_and, n32_bit_and_6__4_bit_out_and,
       n32_bit_and_7__4_bit_out_and, n32_bit_and_8__4_bit_out_and, n32_bit_and_9__4_bit_out_and,
       n32_bit_and_10__4_bit_out_and, n32_bit_and_11__4_bit_out_and, n32_bit_and_12__4_bit_out_and,
       n32_bit_and_13__4_bit_out_and, n32_bit_and_14__4_bit_out_and, n32_bit_and_15__4_bit_out_and,
       n32_bit_and_16__4_bit_out_and, n32_bit_fulladder_1_sum, n32_bit_fulladder_2_sum,
       n32_bit_fulladder_3_sum, n32_bit_fulladder_4_sum, n32_bit_fulladder_5_sum, n32_bit_fulladder_6_sum,
       n32_bit_fulladder_7_sum, n32_bit_fulladder_8_sum, n32_bit_fulladder_9_sum, n32_bit_fulladder_10_sum,
       n32_bit_fulladder_11_sum, n32_bit_fulladder_12_sum, n32_bit_fulladder_13_sum,
       n32_bit_fulladder_14_sum, n32_bit_fulladder_15_sum, n32_bit_fulladder_16_sum,
       n32_bit_shift_for_mult_1_a_out, n32_bit_shift_for_mult_1_b_out, n32_bit_shift_for_mult_2_a_out,
       n32_bit_shift_for_mult_2_b_out, n32_bit_shift_for_mult_3_a_out, n32_bit_shift_for_mult_3_b_out,
       n32_bit_shift_for_mult_4_a_out, n32_bit_shift_for_mult_4_b_out, n32_bit_shift_for_mult_5_a_out,
       n32_bit_shift_for_mult_5_b_out, n32_bit_shift_for_mult_6_a_out, n32_bit_shift_for_mult_6_b_out,
       n32_bit_shift_for_mult_7_a_out, n32_bit_shift_for_mult_7_b_out, n32_bit_shift_for_mult_8_a_out,
       n32_bit_shift_for_mult_8_b_out, n32_bit_shift_for_mult_9_a_out, n32_bit_shift_for_mult_9_b_out,
       n32_bit_shift_for_mult_10_a_out, n32_bit_shift_for_mult_10_b_out, n32_bit_shift_for_mult_11_a_out,
       n32_bit_shift_for_mult_11_b_out, n32_bit_shift_for_mult_12_a_out, n32_bit_shift_for_mult_12_b_out,
       n32_bit_shift_for_mult_13_a_out, n32_bit_shift_for_mult_13_b_out, n32_bit_shift_for_mult_14_a_out,
       n32_bit_shift_for_mult_14_b_out;

  assign bit_extender_1_out = {{31{B[0]}}, B[0]};  // Bit_Extender bit_extender_1
  assign bit_extender_2_out = {{31{B[8]}}, B[8]};  // Bit_Extender bit_extender_2
  _32_BIT_AND u_32_bit_and_1 (.A(bit_extender_1_out), .B(A), ._4_BIT_OUT_AND(n32_bit_and_1__4_bit_out_and));
  _32_BIT_AND u_32_bit_and_2 (.A(bit_extender_2_out), .B(A), ._4_BIT_OUT_AND(n32_bit_and_2__4_bit_out_and));
  _32_BIT_FULLADDER u_32_bit_fulladder_1 (
    .Carry(1'b0), .A(n32_bit_and_1__4_bit_out_and), .B({32{1'b0}}), .Sum(n32_bit_fulladder_1_sum));  // open: Carry_Out
  _32_BIT_FULLADDER u_32_bit_fulladder_2 (
    .Carry(1'b0), .A(n32_bit_and_2__4_bit_out_and), .B(line1), .Sum(n32_bit_fulladder_2_sum));  // open: Carry_Out
  _32_BIT_SHIFT_FOR_MULT u_32_bit_shift_for_mult_1 (
    .in_1(B), .in_2(n32_bit_fulladder_1_sum), .B_OUT(n32_bit_shift_for_mult_1_b_out),
    .A_OUT(n32_bit_shift_for_mult_1_a_out));
  _32_BIT_SHIFT_FOR_MULT u_32_bit_shift_for_mult_2 (
    .in_1(line2), .in_2(n32_bit_fulladder_2_sum), .B_OUT(n32_bit_shift_for_mult_2_b_out),
    .A_OUT(n32_bit_shift_for_mult_2_a_out));
  assign bit_extender_3_out = {{31{B[1]}}, B[1]};  // Bit_Extender bit_extender_3
  assign bit_extender_4_out = {{31{B[9]}}, B[9]};  // Bit_Extender bit_extender_4
  _32_BIT_AND u_32_bit_and_3 (.A(bit_extender_3_out), .B(A), ._4_BIT_OUT_AND(n32_bit_and_3__4_bit_out_and));
  _32_BIT_AND u_32_bit_and_4 (.A(bit_extender_4_out), .B(A), ._4_BIT_OUT_AND(n32_bit_and_4__4_bit_out_and));
  _32_BIT_FULLADDER u_32_bit_fulladder_3 (
    .Carry(1'b0), .A(n32_bit_and_3__4_bit_out_and), .B(n32_bit_shift_for_mult_1_b_out),
    .Sum(n32_bit_fulladder_3_sum));  // open: Carry_Out
  _32_BIT_FULLADDER u_32_bit_fulladder_4 (
    .Carry(1'b0), .A(n32_bit_and_4__4_bit_out_and), .B(n32_bit_shift_for_mult_2_b_out),
    .Sum(n32_bit_fulladder_4_sum));  // open: Carry_Out
  _32_BIT_SHIFT_FOR_MULT u_32_bit_shift_for_mult_3 (
    .in_1(n32_bit_shift_for_mult_1_a_out), .in_2(n32_bit_fulladder_3_sum),
    .B_OUT(n32_bit_shift_for_mult_3_b_out), .A_OUT(n32_bit_shift_for_mult_3_a_out));
  _32_BIT_SHIFT_FOR_MULT u_32_bit_shift_for_mult_4 (
    .in_1(n32_bit_shift_for_mult_2_a_out), .in_2(n32_bit_fulladder_4_sum),
    .B_OUT(n32_bit_shift_for_mult_4_b_out), .A_OUT(n32_bit_shift_for_mult_4_a_out));
  assign bit_extender_5_out = {{31{B[2]}}, B[2]};  // Bit_Extender bit_extender_5
  assign bit_extender_6_out = {{31{B[10]}}, B[10]};  // Bit_Extender bit_extender_6
  _32_BIT_AND u_32_bit_and_5 (.A(bit_extender_5_out), .B(A), ._4_BIT_OUT_AND(n32_bit_and_5__4_bit_out_and));
  _32_BIT_AND u_32_bit_and_6 (.A(bit_extender_6_out), .B(A), ._4_BIT_OUT_AND(n32_bit_and_6__4_bit_out_and));
  _32_BIT_FULLADDER u_32_bit_fulladder_5 (
    .Carry(1'b0), .A(n32_bit_and_5__4_bit_out_and), .B(n32_bit_shift_for_mult_3_b_out),
    .Sum(n32_bit_fulladder_5_sum));  // open: Carry_Out
  _32_BIT_FULLADDER u_32_bit_fulladder_6 (
    .Carry(1'b0), .A(n32_bit_and_6__4_bit_out_and), .B(n32_bit_shift_for_mult_4_b_out),
    .Sum(n32_bit_fulladder_6_sum));  // open: Carry_Out
  _32_BIT_SHIFT_FOR_MULT u_32_bit_shift_for_mult_5 (
    .in_1(n32_bit_shift_for_mult_3_a_out), .in_2(n32_bit_fulladder_5_sum),
    .B_OUT(n32_bit_shift_for_mult_5_b_out), .A_OUT(n32_bit_shift_for_mult_5_a_out));
  _32_BIT_SHIFT_FOR_MULT u_32_bit_shift_for_mult_6 (
    .in_1(n32_bit_shift_for_mult_4_a_out), .in_2(n32_bit_fulladder_6_sum),
    .B_OUT(n32_bit_shift_for_mult_6_b_out), .A_OUT(n32_bit_shift_for_mult_6_a_out));
  assign bit_extender_7_out = {{31{B[3]}}, B[3]};  // Bit_Extender bit_extender_7
  assign bit_extender_8_out = {{31{B[11]}}, B[11]};  // Bit_Extender bit_extender_8
  _32_BIT_AND u_32_bit_and_7 (.A(bit_extender_7_out), .B(A), ._4_BIT_OUT_AND(n32_bit_and_7__4_bit_out_and));
  _32_BIT_AND u_32_bit_and_8 (.A(bit_extender_8_out), .B(A), ._4_BIT_OUT_AND(n32_bit_and_8__4_bit_out_and));
  _32_BIT_FULLADDER u_32_bit_fulladder_7 (
    .Carry(1'b0), .A(n32_bit_and_7__4_bit_out_and), .B(n32_bit_shift_for_mult_5_b_out),
    .Sum(n32_bit_fulladder_7_sum));  // open: Carry_Out
  _32_BIT_FULLADDER u_32_bit_fulladder_8 (
    .Carry(1'b0), .A(n32_bit_and_8__4_bit_out_and), .B(n32_bit_shift_for_mult_6_b_out),
    .Sum(n32_bit_fulladder_8_sum));  // open: Carry_Out
  _32_BIT_SHIFT_FOR_MULT u_32_bit_shift_for_mult_7 (
    .in_1(n32_bit_shift_for_mult_5_a_out), .in_2(n32_bit_fulladder_7_sum),
    .B_OUT(n32_bit_shift_for_mult_7_b_out), .A_OUT(n32_bit_shift_for_mult_7_a_out));
  _32_BIT_SHIFT_FOR_MULT u_32_bit_shift_for_mult_8 (
    .in_1(n32_bit_shift_for_mult_6_a_out), .in_2(n32_bit_fulladder_8_sum),
    .B_OUT(n32_bit_shift_for_mult_8_b_out), .A_OUT(n32_bit_shift_for_mult_8_a_out));
  assign bit_extender_9_out = {{31{B[4]}}, B[4]};  // Bit_Extender bit_extender_9
  assign bit_extender_10_out = {{31{B[12]}}, B[12]};  // Bit_Extender bit_extender_10
  _32_BIT_AND u_32_bit_and_9 (.A(bit_extender_9_out), .B(A), ._4_BIT_OUT_AND(n32_bit_and_9__4_bit_out_and));
  _32_BIT_AND u_32_bit_and_10 (.A(bit_extender_10_out), .B(A), ._4_BIT_OUT_AND(n32_bit_and_10__4_bit_out_and));
  // Probe on nothing
  _32_BIT_FULLADDER u_32_bit_fulladder_9 (
    .Carry(1'b0), .A(n32_bit_and_9__4_bit_out_and), .B(n32_bit_shift_for_mult_7_b_out),
    .Sum(n32_bit_fulladder_9_sum));  // open: Carry_Out
  _32_BIT_FULLADDER u_32_bit_fulladder_10 (
    .Carry(1'b0), .A(n32_bit_and_10__4_bit_out_and), .B(n32_bit_shift_for_mult_8_b_out),
    .Sum(n32_bit_fulladder_10_sum));  // open: Carry_Out
  _32_BIT_SHIFT_FOR_MULT u_32_bit_shift_for_mult_9 (
    .in_1(n32_bit_shift_for_mult_7_a_out), .in_2(n32_bit_fulladder_9_sum),
    .B_OUT(n32_bit_shift_for_mult_9_b_out), .A_OUT(n32_bit_shift_for_mult_9_a_out));
  _32_BIT_SHIFT_FOR_MULT u_32_bit_shift_for_mult_10 (
    .in_1(n32_bit_shift_for_mult_8_a_out), .in_2(n32_bit_fulladder_10_sum),
    .B_OUT(n32_bit_shift_for_mult_10_b_out), .A_OUT(n32_bit_shift_for_mult_10_a_out));
  assign bit_extender_11_out = {{31{B[5]}}, B[5]};  // Bit_Extender bit_extender_11
  assign bit_extender_12_out = {{31{B[13]}}, B[13]};  // Bit_Extender bit_extender_12
  _32_BIT_AND u_32_bit_and_11 (.A(bit_extender_11_out), .B(A), ._4_BIT_OUT_AND(n32_bit_and_11__4_bit_out_and));
  _32_BIT_AND u_32_bit_and_12 (.A(bit_extender_12_out), .B(A), ._4_BIT_OUT_AND(n32_bit_and_12__4_bit_out_and));
  _32_BIT_FULLADDER u_32_bit_fulladder_11 (
    .Carry(1'b0), .A(n32_bit_and_11__4_bit_out_and), .B(n32_bit_shift_for_mult_9_b_out),
    .Sum(n32_bit_fulladder_11_sum));  // open: Carry_Out
  _32_BIT_FULLADDER u_32_bit_fulladder_12 (
    .Carry(1'b0), .A(n32_bit_and_12__4_bit_out_and), .B(n32_bit_shift_for_mult_10_b_out),
    .Sum(n32_bit_fulladder_12_sum));  // open: Carry_Out
  _32_BIT_SHIFT_FOR_MULT u_32_bit_shift_for_mult_11 (
    .in_1(n32_bit_shift_for_mult_9_a_out), .in_2(n32_bit_fulladder_11_sum),
    .B_OUT(n32_bit_shift_for_mult_11_b_out), .A_OUT(n32_bit_shift_for_mult_11_a_out));
  _32_BIT_SHIFT_FOR_MULT u_32_bit_shift_for_mult_12 (
    .in_1(n32_bit_shift_for_mult_10_a_out), .in_2(n32_bit_fulladder_12_sum),
    .B_OUT(n32_bit_shift_for_mult_12_b_out), .A_OUT(n32_bit_shift_for_mult_12_a_out));
  assign bit_extender_13_out = {{31{B[6]}}, B[6]};  // Bit_Extender bit_extender_13
  assign bit_extender_14_out = {{31{B[14]}}, B[14]};  // Bit_Extender bit_extender_14
  _32_BIT_AND u_32_bit_and_13 (.A(bit_extender_13_out), .B(A), ._4_BIT_OUT_AND(n32_bit_and_13__4_bit_out_and));
  _32_BIT_AND u_32_bit_and_14 (.A(bit_extender_14_out), .B(A), ._4_BIT_OUT_AND(n32_bit_and_14__4_bit_out_and));
  _32_BIT_FULLADDER u_32_bit_fulladder_13 (
    .Carry(1'b0), .A(n32_bit_and_13__4_bit_out_and), .B(n32_bit_shift_for_mult_11_b_out),
    .Sum(n32_bit_fulladder_13_sum));  // open: Carry_Out
  _32_BIT_FULLADDER u_32_bit_fulladder_14 (
    .Carry(1'b0), .A(n32_bit_and_14__4_bit_out_and), .B(n32_bit_shift_for_mult_12_b_out),
    .Sum(n32_bit_fulladder_14_sum));  // open: Carry_Out
  _32_BIT_SHIFT_FOR_MULT u_32_bit_shift_for_mult_13 (
    .in_1(n32_bit_shift_for_mult_11_a_out), .in_2(n32_bit_fulladder_13_sum),
    .B_OUT(n32_bit_shift_for_mult_13_b_out), .A_OUT(n32_bit_shift_for_mult_13_a_out));
  _32_BIT_SHIFT_FOR_MULT u_32_bit_shift_for_mult_14 (
    .in_1(n32_bit_shift_for_mult_12_a_out), .in_2(n32_bit_fulladder_14_sum),
    .B_OUT(n32_bit_shift_for_mult_14_b_out), .A_OUT(n32_bit_shift_for_mult_14_a_out));
  assign bit_extender_15_out = {{31{B[7]}}, B[7]};  // Bit_Extender bit_extender_15
  assign bit_extender_16_out = {{31{B[15]}}, B[15]};  // Bit_Extender bit_extender_16
  _32_BIT_AND u_32_bit_and_15 (.A(bit_extender_15_out), .B(A), ._4_BIT_OUT_AND(n32_bit_and_15__4_bit_out_and));
  _32_BIT_AND u_32_bit_and_16 (.A(bit_extender_16_out), .B(A), ._4_BIT_OUT_AND(n32_bit_and_16__4_bit_out_and));
  _32_BIT_FULLADDER u_32_bit_fulladder_15 (
    .Carry(1'b0), .A(n32_bit_and_15__4_bit_out_and), .B(n32_bit_shift_for_mult_13_b_out),
    .Sum(n32_bit_fulladder_15_sum));  // open: Carry_Out
  _32_BIT_FULLADDER u_32_bit_fulladder_16 (
    .Carry(1'b0), .A(n32_bit_and_16__4_bit_out_and), .B(n32_bit_shift_for_mult_14_b_out),
    .Sum(n32_bit_fulladder_16_sum));  // open: Carry_Out
  _32_BIT_SHIFT_FOR_MULT u_32_bit_shift_for_mult_15 (
    .in_1(n32_bit_shift_for_mult_13_a_out), .in_2(n32_bit_fulladder_15_sum), .B_OUT(line1), .A_OUT(line2));
  _32_BIT_SHIFT_FOR_MULT u_32_bit_shift_for_mult_16 (
    .in_1(n32_bit_shift_for_mult_14_a_out), .in_2(n32_bit_fulladder_16_sum),
    .A_OUT({B_OUT[15:0], B_OUT[31:16]}));  // open: B_OUT
endmodule

module _32_BIT_AND (
  input  [31:0] A,
  input  [31:0] B,
  output [31:0] _4_BIT_OUT_AND
);

  and and_1 (_4_BIT_OUT_AND[0], A[0], B[0]);
  and and_2 (_4_BIT_OUT_AND[1], A[1], B[1]);
  and and_3 (_4_BIT_OUT_AND[2], A[2], B[2]);
  and and_4 (_4_BIT_OUT_AND[3], A[3], B[3]);
  and and_5 (_4_BIT_OUT_AND[4], A[4], B[4]);
  and and_6 (_4_BIT_OUT_AND[5], A[5], B[5]);
  and and_7 (_4_BIT_OUT_AND[6], A[6], B[6]);
  and and_8 (_4_BIT_OUT_AND[7], A[7], B[7]);
  and and_9 (_4_BIT_OUT_AND[8], A[8], B[8]);
  and and_10 (_4_BIT_OUT_AND[9], A[9], B[9]);
  and and_11 (_4_BIT_OUT_AND[10], A[10], B[10]);
  and and_12 (_4_BIT_OUT_AND[11], A[11], B[11]);
  and and_13 (_4_BIT_OUT_AND[12], A[12], B[12]);
  and and_14 (_4_BIT_OUT_AND[13], A[13], B[13]);
  and and_15 (_4_BIT_OUT_AND[14], A[14], B[14]);
  and and_16 (_4_BIT_OUT_AND[15], A[15], B[15]);
  and and_17 (_4_BIT_OUT_AND[16], A[16], B[16]);
  and and_18 (_4_BIT_OUT_AND[17], A[17], B[17]);
  and and_19 (_4_BIT_OUT_AND[18], A[18], B[18]);
  and and_20 (_4_BIT_OUT_AND[19], A[19], B[19]);
  and and_21 (_4_BIT_OUT_AND[20], A[20], B[20]);
  and and_22 (_4_BIT_OUT_AND[21], A[21], B[21]);
  and and_23 (_4_BIT_OUT_AND[22], A[22], B[22]);
  and and_24 (_4_BIT_OUT_AND[23], A[23], B[23]);
  and and_25 (_4_BIT_OUT_AND[24], A[24], B[24]);
  and and_26 (_4_BIT_OUT_AND[25], A[25], B[25]);
  and and_27 (_4_BIT_OUT_AND[26], A[26], B[26]);
  and and_28 (_4_BIT_OUT_AND[27], A[27], B[27]);
  and and_29 (_4_BIT_OUT_AND[28], A[28], B[28]);
  and and_30 (_4_BIT_OUT_AND[29], A[29], B[29]);
  and and_31 (_4_BIT_OUT_AND[30], A[30], B[30]);
  and and_32 (_4_BIT_OUT_AND[31], A[31], B[31]);
endmodule

module _32_BIT_OR (
  input  [31:0] A,
  input  [31:0] B,
  output [31:0] _4_BIT_OUT_AND
);

  or or_1 (_4_BIT_OUT_AND[0], A[0], B[0]);
  or or_2 (_4_BIT_OUT_AND[1], A[1], B[1]);
  or or_3 (_4_BIT_OUT_AND[2], A[2], B[2]);
  or or_4 (_4_BIT_OUT_AND[3], A[3], B[3]);
  or or_5 (_4_BIT_OUT_AND[4], A[4], B[4]);
  or or_6 (_4_BIT_OUT_AND[5], A[5], B[5]);
  or or_7 (_4_BIT_OUT_AND[6], A[6], B[6]);
  or or_8 (_4_BIT_OUT_AND[7], A[7], B[7]);
  or or_9 (_4_BIT_OUT_AND[8], A[8], B[8]);
  or or_10 (_4_BIT_OUT_AND[9], A[9], B[9]);
  or or_11 (_4_BIT_OUT_AND[10], A[10], B[10]);
  or or_12 (_4_BIT_OUT_AND[11], A[11], B[11]);
  or or_13 (_4_BIT_OUT_AND[12], A[12], B[12]);
  or or_14 (_4_BIT_OUT_AND[13], A[13], B[13]);
  or or_15 (_4_BIT_OUT_AND[14], A[14], B[14]);
  or or_16 (_4_BIT_OUT_AND[15], A[15], B[15]);
  or or_17 (_4_BIT_OUT_AND[16], A[16], B[16]);
  or or_18 (_4_BIT_OUT_AND[17], A[17], B[17]);
  or or_19 (_4_BIT_OUT_AND[18], A[18], B[18]);
  or or_20 (_4_BIT_OUT_AND[19], A[19], B[19]);
  or or_21 (_4_BIT_OUT_AND[20], A[20], B[20]);
  or or_22 (_4_BIT_OUT_AND[21], A[21], B[21]);
  or or_23 (_4_BIT_OUT_AND[22], A[22], B[22]);
  or or_24 (_4_BIT_OUT_AND[23], A[23], B[23]);
  or or_25 (_4_BIT_OUT_AND[24], A[24], B[24]);
  or or_26 (_4_BIT_OUT_AND[25], A[25], B[25]);
  or or_27 (_4_BIT_OUT_AND[26], A[26], B[26]);
  or or_28 (_4_BIT_OUT_AND[27], A[27], B[27]);
  or or_29 (_4_BIT_OUT_AND[28], A[28], B[28]);
  or or_30 (_4_BIT_OUT_AND[29], A[29], B[29]);
  or or_31 (_4_BIT_OUT_AND[30], A[30], B[30]);
  or or_32 (_4_BIT_OUT_AND[31], A[31], B[31]);
endmodule

module _32_BIT_XOR (
  input  [31:0] A,
  input  [31:0] B,
  output [31:0] _4_BIT_OUT_AND
);

  xor xor_1 (_4_BIT_OUT_AND[0], A[0], B[0]);
  xor xor_2 (_4_BIT_OUT_AND[1], A[1], B[1]);
  xor xor_3 (_4_BIT_OUT_AND[2], A[2], B[2]);
  xor xor_4 (_4_BIT_OUT_AND[3], A[3], B[3]);
  xor xor_5 (_4_BIT_OUT_AND[4], A[4], B[4]);
  xor xor_6 (_4_BIT_OUT_AND[5], A[5], B[5]);
  xor xor_7 (_4_BIT_OUT_AND[6], A[6], B[6]);
  xor xor_8 (_4_BIT_OUT_AND[7], A[7], B[7]);
  xor xor_9 (_4_BIT_OUT_AND[8], A[8], B[8]);
  xor xor_10 (_4_BIT_OUT_AND[9], A[9], B[9]);
  xor xor_11 (_4_BIT_OUT_AND[10], A[10], B[10]);
  xor xor_12 (_4_BIT_OUT_AND[11], A[11], B[11]);
  xor xor_13 (_4_BIT_OUT_AND[12], A[12], B[12]);
  xor xor_14 (_4_BIT_OUT_AND[13], A[13], B[13]);
  xor xor_15 (_4_BIT_OUT_AND[14], A[14], B[14]);
  xor xor_16 (_4_BIT_OUT_AND[15], A[15], B[15]);
  xor xor_17 (_4_BIT_OUT_AND[16], A[16], B[16]);
  xor xor_18 (_4_BIT_OUT_AND[17], A[17], B[17]);
  xor xor_19 (_4_BIT_OUT_AND[18], A[18], B[18]);
  xor xor_20 (_4_BIT_OUT_AND[19], A[19], B[19]);
  xor xor_21 (_4_BIT_OUT_AND[20], A[20], B[20]);
  xor xor_22 (_4_BIT_OUT_AND[21], A[21], B[21]);
  xor xor_23 (_4_BIT_OUT_AND[22], A[22], B[22]);
  xor xor_24 (_4_BIT_OUT_AND[23], A[23], B[23]);
  xor xor_25 (_4_BIT_OUT_AND[24], A[24], B[24]);
  xor xor_26 (_4_BIT_OUT_AND[25], A[25], B[25]);
  xor xor_27 (_4_BIT_OUT_AND[26], A[26], B[26]);
  xor xor_28 (_4_BIT_OUT_AND[27], A[27], B[27]);
  xor xor_29 (_4_BIT_OUT_AND[28], A[28], B[28]);
  xor xor_30 (_4_BIT_OUT_AND[29], A[29], B[29]);
  xor xor_31 (_4_BIT_OUT_AND[30], A[30], B[30]);
  xor xor_32 (_4_BIT_OUT_AND[31], A[31], B[31]);
endmodule

module _32_BIT_SHIFT_LEFT (
  input  [31:0] A,
  input  [31:0] B,
  output [31:0] Sum
);

  wire multiplexer_1_out, multiplexer_2_out, multiplexer_3_out, multiplexer_4_out, multiplexer_5_out,
       multiplexer_6_out, multiplexer_7_out, multiplexer_8_out, multiplexer_9_out, multiplexer_10_out,
       multiplexer_11_out, multiplexer_12_out, multiplexer_13_out, multiplexer_14_out, multiplexer_15_out,
       multiplexer_16_out, multiplexer_17_out, multiplexer_18_out, multiplexer_19_out, multiplexer_20_out,
       multiplexer_21_out, multiplexer_22_out, multiplexer_23_out, multiplexer_24_out, multiplexer_25_out,
       multiplexer_26_out, multiplexer_27_out, multiplexer_28_out, multiplexer_29_out, multiplexer_30_out,
       multiplexer_31_out, multiplexer_32_out, multiplexer_33_out, multiplexer_34_out, multiplexer_35_out,
       multiplexer_36_out, multiplexer_37_out, multiplexer_38_out, multiplexer_39_out, multiplexer_40_out,
       multiplexer_41_out, multiplexer_42_out, multiplexer_43_out, multiplexer_44_out, multiplexer_45_out,
       multiplexer_46_out, multiplexer_47_out, multiplexer_48_out, multiplexer_49_out, multiplexer_50_out,
       multiplexer_51_out, multiplexer_52_out, multiplexer_53_out, multiplexer_54_out, multiplexer_55_out,
       multiplexer_56_out, multiplexer_57_out, multiplexer_58_out, multiplexer_59_out, multiplexer_60_out,
       multiplexer_61_out, multiplexer_62_out, multiplexer_63_out, multiplexer_64_out, multiplexer_65_out,
       multiplexer_66_out, multiplexer_67_out, multiplexer_68_out, multiplexer_69_out, multiplexer_70_out,
       multiplexer_71_out, multiplexer_72_out, multiplexer_73_out, multiplexer_74_out, multiplexer_75_out,
       multiplexer_76_out, multiplexer_77_out, multiplexer_78_out, multiplexer_79_out, multiplexer_80_out,
       multiplexer_81_out, multiplexer_82_out, multiplexer_83_out, multiplexer_84_out, multiplexer_85_out,
       multiplexer_86_out, multiplexer_87_out, multiplexer_88_out, multiplexer_89_out, multiplexer_90_out,
       multiplexer_91_out, multiplexer_92_out, multiplexer_93_out, multiplexer_94_out, multiplexer_95_out,
       multiplexer_96_out, multiplexer_97_out, multiplexer_98_out, multiplexer_99_out, multiplexer_100_out,
       multiplexer_101_out, multiplexer_102_out, multiplexer_103_out, multiplexer_104_out,
       multiplexer_105_out, multiplexer_106_out, multiplexer_107_out, multiplexer_108_out,
       multiplexer_109_out, multiplexer_110_out, multiplexer_111_out, multiplexer_112_out,
       multiplexer_113_out, multiplexer_114_out, multiplexer_115_out, multiplexer_116_out,
       multiplexer_117_out, multiplexer_118_out, multiplexer_119_out, multiplexer_120_out,
       multiplexer_121_out, multiplexer_122_out, multiplexer_123_out, multiplexer_124_out,
       multiplexer_125_out, multiplexer_126_out, multiplexer_127_out, multiplexer_128_out, not_1_out;

  Multiplexer #(.enable("false")) multiplexer_1 (.in0(1'b0), .in1(A[0]), .out(multiplexer_1_out), .sel(not_1_out));
  Multiplexer #(.enable("false")) multiplexer_2 (.in0(A[0]), .in1(A[1]), .out(multiplexer_2_out), .sel(not_1_out));
  Multiplexer #(.enable("false")) multiplexer_3 (.in0(A[1]), .in1(A[2]), .out(multiplexer_3_out), .sel(not_1_out));
  Multiplexer #(.enable("false")) multiplexer_4 (.in0(A[2]), .in1(A[3]), .out(multiplexer_4_out), .sel(not_1_out));
  Multiplexer #(.enable("false")) multiplexer_5 (.in0(A[3]), .in1(A[4]), .out(multiplexer_5_out), .sel(not_1_out));
  Multiplexer #(.enable("false")) multiplexer_6 (.in0(A[4]), .in1(A[5]), .out(multiplexer_6_out), .sel(not_1_out));
  Multiplexer #(.enable("false")) multiplexer_7 (.in0(A[5]), .in1(A[6]), .out(multiplexer_7_out), .sel(not_1_out));
  Multiplexer #(.enable("false")) multiplexer_8 (.in0(A[6]), .in1(A[7]), .out(multiplexer_8_out), .sel(not_1_out));
  Multiplexer #(.enable("false")) multiplexer_9 (.in0(A[7]), .in1(A[8]), .out(multiplexer_9_out), .sel(not_1_out));
  Multiplexer #(.enable("false")) multiplexer_10 (.in0(A[8]), .in1(A[9]), .out(multiplexer_10_out), .sel(not_1_out));
  Multiplexer #(.enable("false")) multiplexer_11 (.in0(A[9]), .in1(A[10]), .out(multiplexer_11_out), .sel(not_1_out));
  Multiplexer #(.enable("false")) multiplexer_12 (.in0(A[10]), .in1(A[11]), .out(multiplexer_12_out), .sel(not_1_out));
  Multiplexer #(.enable("false")) multiplexer_13 (.in0(A[11]), .in1(A[12]), .out(multiplexer_13_out), .sel(not_1_out));
  Multiplexer #(.enable("false")) multiplexer_14 (.in0(A[12]), .in1(A[13]), .out(multiplexer_14_out), .sel(not_1_out));
  Multiplexer #(.enable("false")) multiplexer_15 (.in0(A[13]), .in1(A[14]), .out(multiplexer_15_out), .sel(not_1_out));
  Multiplexer #(.enable("false")) multiplexer_16 (.in0(A[14]), .in1(A[15]), .out(multiplexer_16_out), .sel(not_1_out));
  Multiplexer #(.enable("false")) multiplexer_17 (.in0(A[15]), .in1(A[16]), .out(multiplexer_17_out), .sel(not_1_out));
  Multiplexer #(.enable("false")) multiplexer_18 (.in0(A[16]), .in1(A[17]), .out(multiplexer_18_out), .sel(not_1_out));
  Multiplexer #(.enable("false")) multiplexer_19 (.in0(A[17]), .in1(A[18]), .out(multiplexer_19_out), .sel(not_1_out));
  Multiplexer #(.enable("false")) multiplexer_20 (.in0(A[18]), .in1(A[19]), .out(multiplexer_20_out), .sel(not_1_out));
  Multiplexer #(.enable("false")) multiplexer_21 (.in0(A[19]), .in1(A[20]), .out(multiplexer_21_out), .sel(not_1_out));
  Multiplexer #(.enable("false")) multiplexer_22 (.in0(A[20]), .in1(A[21]), .out(multiplexer_22_out), .sel(not_1_out));
  Multiplexer #(.enable("false")) multiplexer_23 (.in0(A[21]), .in1(A[22]), .out(multiplexer_23_out), .sel(not_1_out));
  Multiplexer #(.enable("false")) multiplexer_24 (.in0(A[22]), .in1(A[23]), .out(multiplexer_24_out), .sel(not_1_out));
  Multiplexer #(.enable("false")) multiplexer_25 (.in0(A[23]), .in1(A[24]), .out(multiplexer_25_out), .sel(not_1_out));
  Multiplexer #(.enable("false")) multiplexer_26 (.in0(A[24]), .in1(A[25]), .out(multiplexer_26_out), .sel(not_1_out));
  Multiplexer #(.enable("false")) multiplexer_27 (.in0(A[25]), .in1(A[26]), .out(multiplexer_27_out), .sel(not_1_out));
  Multiplexer #(.enable("false")) multiplexer_28 (.in0(A[26]), .in1(A[27]), .out(multiplexer_28_out), .sel(not_1_out));
  Multiplexer #(.enable("false")) multiplexer_29 (.in0(A[27]), .in1(A[28]), .out(multiplexer_29_out), .sel(not_1_out));
  Multiplexer #(.enable("false")) multiplexer_30 (.in0(A[28]), .in1(A[29]), .out(multiplexer_30_out), .sel(not_1_out));
  Multiplexer #(.enable("false")) multiplexer_31 (.in0(A[29]), .in1(A[30]), .out(multiplexer_31_out), .sel(not_1_out));
  Multiplexer #(.enable("false")) multiplexer_32 (.in0(A[30]), .in1(A[31]), .out(multiplexer_32_out), .sel(not_1_out));
  not not_1 (not_1_out, B[0]);
  Multiplexer #(.enable("false")) multiplexer_33 (
    .in0(multiplexer_1_out), .in1(1'b0), .out(multiplexer_33_out), .sel(B[1]));
  Multiplexer #(.enable("false")) multiplexer_34 (
    .in0(multiplexer_2_out), .in1(1'b0), .out(multiplexer_34_out), .sel(B[1]));
  Multiplexer #(.enable("false")) multiplexer_35 (
    .in0(multiplexer_3_out), .in1(multiplexer_1_out), .out(multiplexer_35_out), .sel(B[1]));
  Multiplexer #(.enable("false")) multiplexer_36 (
    .in0(multiplexer_4_out), .in1(multiplexer_2_out), .out(multiplexer_36_out), .sel(B[1]));
  Multiplexer #(.enable("false")) multiplexer_37 (
    .in0(multiplexer_5_out), .in1(multiplexer_3_out), .out(multiplexer_37_out), .sel(B[1]));
  Multiplexer #(.enable("false")) multiplexer_38 (
    .in0(multiplexer_6_out), .in1(multiplexer_4_out), .out(multiplexer_38_out), .sel(B[1]));
  Multiplexer #(.enable("false")) multiplexer_39 (
    .in0(multiplexer_7_out), .in1(multiplexer_5_out), .out(multiplexer_39_out), .sel(B[1]));
  Multiplexer #(.enable("false")) multiplexer_40 (
    .in0(multiplexer_8_out), .in1(multiplexer_6_out), .out(multiplexer_40_out), .sel(B[1]));
  Multiplexer #(.enable("false")) multiplexer_41 (
    .in0(multiplexer_9_out), .in1(multiplexer_7_out), .out(multiplexer_41_out), .sel(B[1]));
  Multiplexer #(.enable("false")) multiplexer_42 (
    .in0(multiplexer_10_out), .in1(multiplexer_8_out), .out(multiplexer_42_out), .sel(B[1]));
  Multiplexer #(.enable("false")) multiplexer_43 (
    .in0(multiplexer_11_out), .in1(multiplexer_9_out), .out(multiplexer_43_out), .sel(B[1]));
  Multiplexer #(.enable("false")) multiplexer_44 (
    .in0(multiplexer_12_out), .in1(multiplexer_10_out), .out(multiplexer_44_out), .sel(B[1]));
  Multiplexer #(.enable("false")) multiplexer_45 (
    .in0(multiplexer_13_out), .in1(multiplexer_11_out), .out(multiplexer_45_out), .sel(B[1]));
  Multiplexer #(.enable("false")) multiplexer_46 (
    .in0(multiplexer_14_out), .in1(multiplexer_12_out), .out(multiplexer_46_out), .sel(B[1]));
  Multiplexer #(.enable("false")) multiplexer_47 (
    .in0(multiplexer_15_out), .in1(multiplexer_13_out), .out(multiplexer_47_out), .sel(B[1]));
  Multiplexer #(.enable("false")) multiplexer_48 (
    .in0(multiplexer_16_out), .in1(multiplexer_14_out), .out(multiplexer_48_out), .sel(B[1]));
  Multiplexer #(.enable("false")) multiplexer_49 (
    .in0(multiplexer_17_out), .in1(multiplexer_15_out), .out(multiplexer_49_out), .sel(B[1]));
  Multiplexer #(.enable("false")) multiplexer_50 (
    .in0(multiplexer_18_out), .in1(multiplexer_16_out), .out(multiplexer_50_out), .sel(B[1]));
  Multiplexer #(.enable("false")) multiplexer_51 (
    .in0(multiplexer_19_out), .in1(multiplexer_17_out), .out(multiplexer_51_out), .sel(B[1]));
  Multiplexer #(.enable("false")) multiplexer_52 (
    .in0(multiplexer_20_out), .in1(multiplexer_18_out), .out(multiplexer_52_out), .sel(B[1]));
  Multiplexer #(.enable("false")) multiplexer_53 (
    .in0(multiplexer_21_out), .in1(multiplexer_19_out), .out(multiplexer_53_out), .sel(B[1]));
  Multiplexer #(.enable("false")) multiplexer_54 (
    .in0(multiplexer_22_out), .in1(multiplexer_20_out), .out(multiplexer_54_out), .sel(B[1]));
  Multiplexer #(.enable("false")) multiplexer_55 (
    .in0(multiplexer_23_out), .in1(multiplexer_21_out), .out(multiplexer_55_out), .sel(B[1]));
  Multiplexer #(.enable("false")) multiplexer_56 (
    .in0(multiplexer_24_out), .in1(multiplexer_22_out), .out(multiplexer_56_out), .sel(B[1]));
  Multiplexer #(.enable("false")) multiplexer_57 (
    .in0(multiplexer_25_out), .in1(multiplexer_23_out), .out(multiplexer_57_out), .sel(B[1]));
  Multiplexer #(.enable("false")) multiplexer_58 (
    .in0(multiplexer_26_out), .in1(multiplexer_24_out), .out(multiplexer_58_out), .sel(B[1]));
  Multiplexer #(.enable("false")) multiplexer_59 (
    .in0(multiplexer_27_out), .in1(multiplexer_25_out), .out(multiplexer_59_out), .sel(B[1]));
  Multiplexer #(.enable("false")) multiplexer_60 (
    .in0(multiplexer_28_out), .in1(multiplexer_26_out), .out(multiplexer_60_out), .sel(B[1]));
  Multiplexer #(.enable("false")) multiplexer_61 (
    .in0(multiplexer_29_out), .in1(multiplexer_27_out), .out(multiplexer_61_out), .sel(B[1]));
  Multiplexer #(.enable("false")) multiplexer_62 (
    .in0(multiplexer_30_out), .in1(multiplexer_28_out), .out(multiplexer_62_out), .sel(B[1]));
  Multiplexer #(.enable("false")) multiplexer_63 (
    .in0(multiplexer_31_out), .in1(multiplexer_29_out), .out(multiplexer_63_out), .sel(B[1]));
  Multiplexer #(.enable("false")) multiplexer_64 (
    .in0(multiplexer_32_out), .in1(multiplexer_30_out), .out(multiplexer_64_out), .sel(B[1]));
  Multiplexer #(.enable("false")) multiplexer_65 (
    .in0(multiplexer_33_out), .in1(1'b0), .out(multiplexer_65_out), .sel(B[2]));
  Multiplexer #(.enable("false")) multiplexer_66 (
    .in0(multiplexer_34_out), .in1(1'b0), .out(multiplexer_66_out), .sel(B[2]));
  Multiplexer #(.enable("false")) multiplexer_67 (
    .in0(multiplexer_35_out), .in1(1'b0), .out(multiplexer_67_out), .sel(B[2]));
  Multiplexer #(.enable("false")) multiplexer_68 (
    .in0(multiplexer_36_out), .in1(1'b0), .out(multiplexer_68_out), .sel(B[2]));
  Multiplexer #(.enable("false")) multiplexer_69 (
    .in0(multiplexer_37_out), .in1(multiplexer_33_out), .out(multiplexer_69_out), .sel(B[2]));
  Multiplexer #(.enable("false")) multiplexer_70 (
    .in0(multiplexer_38_out), .in1(multiplexer_34_out), .out(multiplexer_70_out), .sel(B[2]));
  Multiplexer #(.enable("false")) multiplexer_71 (
    .in0(multiplexer_39_out), .in1(multiplexer_35_out), .out(multiplexer_71_out), .sel(B[2]));
  Multiplexer #(.enable("false")) multiplexer_72 (
    .in0(multiplexer_40_out), .in1(multiplexer_36_out), .out(multiplexer_72_out), .sel(B[2]));
  Multiplexer #(.enable("false")) multiplexer_73 (
    .in0(multiplexer_41_out), .in1(multiplexer_37_out), .out(multiplexer_73_out), .sel(B[2]));
  Multiplexer #(.enable("false")) multiplexer_74 (
    .in0(multiplexer_42_out), .in1(multiplexer_38_out), .out(multiplexer_74_out), .sel(B[2]));
  Multiplexer #(.enable("false")) multiplexer_75 (
    .in0(multiplexer_43_out), .in1(multiplexer_39_out), .out(multiplexer_75_out), .sel(B[2]));
  Multiplexer #(.enable("false")) multiplexer_76 (
    .in0(multiplexer_44_out), .in1(multiplexer_40_out), .out(multiplexer_76_out), .sel(B[2]));
  Multiplexer #(.enable("false")) multiplexer_77 (
    .in0(multiplexer_45_out), .in1(multiplexer_41_out), .out(multiplexer_77_out), .sel(B[2]));
  Multiplexer #(.enable("false")) multiplexer_78 (
    .in0(multiplexer_46_out), .in1(multiplexer_42_out), .out(multiplexer_78_out), .sel(B[2]));
  Multiplexer #(.enable("false")) multiplexer_79 (
    .in0(multiplexer_47_out), .in1(multiplexer_43_out), .out(multiplexer_79_out), .sel(B[2]));
  Multiplexer #(.enable("false")) multiplexer_80 (
    .in0(multiplexer_48_out), .in1(multiplexer_44_out), .out(multiplexer_80_out), .sel(B[2]));
  Multiplexer #(.enable("false")) multiplexer_81 (
    .in0(multiplexer_49_out), .in1(multiplexer_45_out), .out(multiplexer_81_out), .sel(B[2]));
  Multiplexer #(.enable("false")) multiplexer_82 (
    .in0(multiplexer_50_out), .in1(multiplexer_46_out), .out(multiplexer_82_out), .sel(B[2]));
  Multiplexer #(.enable("false")) multiplexer_83 (
    .in0(multiplexer_51_out), .in1(multiplexer_47_out), .out(multiplexer_83_out), .sel(B[2]));
  Multiplexer #(.enable("false")) multiplexer_84 (
    .in0(multiplexer_52_out), .in1(multiplexer_48_out), .out(multiplexer_84_out), .sel(B[2]));
  Multiplexer #(.enable("false")) multiplexer_85 (
    .in0(multiplexer_53_out), .in1(multiplexer_49_out), .out(multiplexer_85_out), .sel(B[2]));
  Multiplexer #(.enable("false")) multiplexer_86 (
    .in0(multiplexer_54_out), .in1(multiplexer_50_out), .out(multiplexer_86_out), .sel(B[2]));
  Multiplexer #(.enable("false")) multiplexer_87 (
    .in0(multiplexer_55_out), .in1(multiplexer_51_out), .out(multiplexer_87_out), .sel(B[2]));
  Multiplexer #(.enable("false")) multiplexer_88 (
    .in0(multiplexer_56_out), .in1(multiplexer_52_out), .out(multiplexer_88_out), .sel(B[2]));
  Multiplexer #(.enable("false")) multiplexer_89 (
    .in0(multiplexer_57_out), .in1(multiplexer_53_out), .out(multiplexer_89_out), .sel(B[2]));
  Multiplexer #(.enable("false")) multiplexer_90 (
    .in0(multiplexer_58_out), .in1(multiplexer_54_out), .out(multiplexer_90_out), .sel(B[2]));
  Multiplexer #(.enable("false")) multiplexer_91 (
    .in0(multiplexer_59_out), .in1(multiplexer_55_out), .out(multiplexer_91_out), .sel(B[2]));
  Multiplexer #(.enable("false")) multiplexer_92 (
    .in0(multiplexer_60_out), .in1(multiplexer_56_out), .out(multiplexer_92_out), .sel(B[2]));
  Multiplexer #(.enable("false")) multiplexer_93 (
    .in0(multiplexer_61_out), .in1(multiplexer_57_out), .out(multiplexer_93_out), .sel(B[2]));
  Multiplexer #(.enable("false")) multiplexer_94 (
    .in0(multiplexer_62_out), .in1(multiplexer_58_out), .out(multiplexer_94_out), .sel(B[2]));
  Multiplexer #(.enable("false")) multiplexer_95 (
    .in0(multiplexer_63_out), .in1(multiplexer_59_out), .out(multiplexer_95_out), .sel(B[2]));
  Multiplexer #(.enable("false")) multiplexer_96 (
    .in0(multiplexer_64_out), .in1(multiplexer_60_out), .out(multiplexer_96_out), .sel(B[2]));
  Multiplexer #(.enable("false")) multiplexer_97 (
    .in0(multiplexer_65_out), .in1(1'b0), .out(multiplexer_97_out), .sel(B[3]));
  Multiplexer #(.enable("false")) multiplexer_98 (
    .in0(multiplexer_66_out), .in1(1'b0), .out(multiplexer_98_out), .sel(B[3]));
  Multiplexer #(.enable("false")) multiplexer_99 (
    .in0(multiplexer_67_out), .in1(1'b0), .out(multiplexer_99_out), .sel(B[3]));
  Multiplexer #(.enable("false")) multiplexer_100 (
    .in0(multiplexer_68_out), .in1(1'b0), .out(multiplexer_100_out), .sel(B[3]));
  Multiplexer #(.enable("false")) multiplexer_101 (
    .in0(multiplexer_69_out), .in1(1'b0), .out(multiplexer_101_out), .sel(B[3]));
  Multiplexer #(.enable("false")) multiplexer_102 (
    .in0(multiplexer_70_out), .in1(1'b0), .out(multiplexer_102_out), .sel(B[3]));
  Multiplexer #(.enable("false")) multiplexer_103 (
    .in0(multiplexer_71_out), .in1(1'b0), .out(multiplexer_103_out), .sel(B[3]));
  Multiplexer #(.enable("false")) multiplexer_104 (
    .in0(multiplexer_72_out), .in1(1'b0), .out(multiplexer_104_out), .sel(B[3]));
  Multiplexer #(.enable("false")) multiplexer_105 (
    .in0(multiplexer_73_out), .in1(multiplexer_65_out), .out(multiplexer_105_out), .sel(B[3]));
  Multiplexer #(.enable("false")) multiplexer_106 (
    .in0(multiplexer_74_out), .in1(multiplexer_66_out), .out(multiplexer_106_out), .sel(B[3]));
  Multiplexer #(.enable("false")) multiplexer_107 (
    .in0(multiplexer_75_out), .in1(multiplexer_67_out), .out(multiplexer_107_out), .sel(B[3]));
  Multiplexer #(.enable("false")) multiplexer_108 (
    .in0(multiplexer_76_out), .in1(multiplexer_68_out), .out(multiplexer_108_out), .sel(B[3]));
  Multiplexer #(.enable("false")) multiplexer_109 (
    .in0(multiplexer_77_out), .in1(multiplexer_69_out), .out(multiplexer_109_out), .sel(B[3]));
  Multiplexer #(.enable("false")) multiplexer_110 (
    .in0(multiplexer_78_out), .in1(multiplexer_70_out), .out(multiplexer_110_out), .sel(B[3]));
  Multiplexer #(.enable("false")) multiplexer_111 (
    .in0(multiplexer_79_out), .in1(multiplexer_71_out), .out(multiplexer_111_out), .sel(B[3]));
  Multiplexer #(.enable("false")) multiplexer_112 (
    .in0(multiplexer_80_out), .in1(multiplexer_72_out), .out(multiplexer_112_out), .sel(B[3]));
  Multiplexer #(.enable("false")) multiplexer_113 (
    .in0(multiplexer_81_out), .in1(multiplexer_73_out), .out(multiplexer_113_out), .sel(B[3]));
  Multiplexer #(.enable("false")) multiplexer_114 (
    .in0(multiplexer_82_out), .in1(multiplexer_74_out), .out(multiplexer_114_out), .sel(B[3]));
  Multiplexer #(.enable("false")) multiplexer_115 (
    .in0(multiplexer_83_out), .in1(multiplexer_75_out), .out(multiplexer_115_out), .sel(B[3]));
  Multiplexer #(.enable("false")) multiplexer_116 (
    .in0(multiplexer_84_out), .in1(multiplexer_76_out), .out(multiplexer_116_out), .sel(B[3]));
  Multiplexer #(.enable("false")) multiplexer_117 (
    .in0(multiplexer_85_out), .in1(multiplexer_77_out), .out(multiplexer_117_out), .sel(B[3]));
  Multiplexer #(.enable("false")) multiplexer_118 (
    .in0(multiplexer_86_out), .in1(multiplexer_78_out), .out(multiplexer_118_out), .sel(B[3]));
  Multiplexer #(.enable("false")) multiplexer_119 (
    .in0(multiplexer_87_out), .in1(multiplexer_79_out), .out(multiplexer_119_out), .sel(B[3]));
  Multiplexer #(.enable("false")) multiplexer_120 (
    .in0(multiplexer_88_out), .in1(multiplexer_80_out), .out(multiplexer_120_out), .sel(B[3]));
  Multiplexer #(.enable("false")) multiplexer_121 (
    .in0(multiplexer_89_out), .in1(multiplexer_81_out), .out(multiplexer_121_out), .sel(B[3]));
  Multiplexer #(.enable("false")) multiplexer_122 (
    .in0(multiplexer_90_out), .in1(multiplexer_82_out), .out(multiplexer_122_out), .sel(B[3]));
  Multiplexer #(.enable("false")) multiplexer_123 (
    .in0(multiplexer_91_out), .in1(multiplexer_83_out), .out(multiplexer_123_out), .sel(B[3]));
  Multiplexer #(.enable("false")) multiplexer_124 (
    .in0(multiplexer_92_out), .in1(multiplexer_84_out), .out(multiplexer_124_out), .sel(B[3]));
  Multiplexer #(.enable("false")) multiplexer_125 (
    .in0(multiplexer_93_out), .in1(multiplexer_85_out), .out(multiplexer_125_out), .sel(B[3]));
  Multiplexer #(.enable("false")) multiplexer_126 (
    .in0(multiplexer_94_out), .in1(multiplexer_86_out), .out(multiplexer_126_out), .sel(B[3]));
  Multiplexer #(.enable("false")) multiplexer_127 (
    .in0(multiplexer_95_out), .in1(multiplexer_87_out), .out(multiplexer_127_out), .sel(B[3]));
  Multiplexer #(.enable("false")) multiplexer_128 (
    .in0(multiplexer_96_out), .in1(multiplexer_88_out), .out(multiplexer_128_out), .sel(B[3]));
  Multiplexer #(.enable("false")) multiplexer_129 (.in0(multiplexer_97_out), .in1(1'b0), .out(Sum[0]), .sel(B[4]));
  Multiplexer #(.enable("false")) multiplexer_130 (.in0(multiplexer_98_out), .in1(1'b0), .out(Sum[1]), .sel(B[4]));
  Multiplexer #(.enable("false")) multiplexer_131 (.in0(multiplexer_99_out), .in1(1'b0), .out(Sum[2]), .sel(B[4]));
  Multiplexer #(.enable("false")) multiplexer_132 (.in0(multiplexer_100_out), .in1(1'b0), .out(Sum[3]), .sel(B[4]));
  Multiplexer #(.enable("false")) multiplexer_133 (.in0(multiplexer_101_out), .in1(1'b0), .out(Sum[4]), .sel(B[4]));
  Multiplexer #(.enable("false")) multiplexer_134 (.in0(multiplexer_102_out), .in1(1'b0), .out(Sum[5]), .sel(B[4]));
  Multiplexer #(.enable("false")) multiplexer_135 (.in0(multiplexer_103_out), .in1(1'b0), .out(Sum[6]), .sel(B[4]));
  Multiplexer #(.enable("false")) multiplexer_136 (.in0(multiplexer_104_out), .in1(1'b0), .out(Sum[7]), .sel(B[4]));
  Multiplexer #(.enable("false")) multiplexer_137 (.in0(multiplexer_105_out), .in1(1'b0), .out(Sum[8]), .sel(B[4]));
  Multiplexer #(.enable("false")) multiplexer_138 (.in0(multiplexer_106_out), .in1(1'b0), .out(Sum[9]), .sel(B[4]));
  Multiplexer #(.enable("false")) multiplexer_139 (.in0(multiplexer_107_out), .in1(1'b0), .out(Sum[10]), .sel(B[4]));
  Multiplexer #(.enable("false")) multiplexer_140 (.in0(multiplexer_108_out), .in1(1'b0), .out(Sum[11]), .sel(B[4]));
  Multiplexer #(.enable("false")) multiplexer_141 (.in0(multiplexer_109_out), .in1(1'b0), .out(Sum[12]), .sel(B[4]));
  Multiplexer #(.enable("false")) multiplexer_142 (.in0(multiplexer_110_out), .in1(1'b0), .out(Sum[13]), .sel(B[4]));
  Multiplexer #(.enable("false")) multiplexer_143 (.in0(multiplexer_111_out), .in1(1'b0), .out(Sum[14]), .sel(B[4]));
  Multiplexer #(.enable("false")) multiplexer_144 (.in0(multiplexer_112_out), .in1(1'b0), .out(Sum[15]), .sel(B[4]));
  Multiplexer #(.enable("false")) multiplexer_145 (
    .in0(multiplexer_113_out), .in1(multiplexer_97_out), .out(Sum[16]), .sel(B[4]));
  Multiplexer #(.enable("false")) multiplexer_146 (
    .in0(multiplexer_114_out), .in1(multiplexer_98_out), .out(Sum[17]), .sel(B[4]));
  Multiplexer #(.enable("false")) multiplexer_147 (
    .in0(multiplexer_115_out), .in1(multiplexer_99_out), .out(Sum[18]), .sel(B[4]));
  Multiplexer #(.enable("false")) multiplexer_148 (
    .in0(multiplexer_116_out), .in1(multiplexer_100_out), .out(Sum[19]), .sel(B[4]));
  Multiplexer #(.enable("false")) multiplexer_149 (
    .in0(multiplexer_117_out), .in1(multiplexer_101_out), .out(Sum[20]), .sel(B[4]));
  Multiplexer #(.enable("false")) multiplexer_150 (
    .in0(multiplexer_118_out), .in1(multiplexer_102_out), .out(Sum[21]), .sel(B[4]));
  Multiplexer #(.enable("false")) multiplexer_151 (
    .in0(multiplexer_119_out), .in1(multiplexer_103_out), .out(Sum[22]), .sel(B[4]));
  Multiplexer #(.enable("false")) multiplexer_152 (
    .in0(multiplexer_120_out), .in1(multiplexer_104_out), .out(Sum[23]), .sel(B[4]));
  Multiplexer #(.enable("false")) multiplexer_153 (
    .in0(multiplexer_121_out), .in1(multiplexer_105_out), .out(Sum[24]), .sel(B[4]));
  Multiplexer #(.enable("false")) multiplexer_154 (
    .in0(multiplexer_122_out), .in1(multiplexer_106_out), .out(Sum[25]), .sel(B[4]));
  Multiplexer #(.enable("false")) multiplexer_155 (
    .in0(multiplexer_123_out), .in1(multiplexer_107_out), .out(Sum[26]), .sel(B[4]));
  Multiplexer #(.enable("false")) multiplexer_156 (
    .in0(multiplexer_124_out), .in1(multiplexer_108_out), .out(Sum[27]), .sel(B[4]));
  Multiplexer #(.enable("false")) multiplexer_157 (
    .in0(multiplexer_125_out), .in1(multiplexer_109_out), .out(Sum[28]), .sel(B[4]));
  Multiplexer #(.enable("false")) multiplexer_158 (
    .in0(multiplexer_126_out), .in1(multiplexer_110_out), .out(Sum[29]), .sel(B[4]));
  Multiplexer #(.enable("false")) multiplexer_159 (
    .in0(multiplexer_127_out), .in1(multiplexer_111_out), .out(Sum[30]), .sel(B[4]));
  Multiplexer #(.enable("false")) multiplexer_160 (
    .in0(multiplexer_128_out), .in1(multiplexer_112_out), .out(Sum[31]), .sel(B[4]));
  // Probe on A
endmodule

module _32_BIT_SET_LESS_THAN (
  input  [31:0] A,
  input  [31:0] B,
  output [31:0] out_3
);

  wire _1, _2, _3, _4, _5, _6, _7, _8, _9, _10, _11, _12, _13, _14, _15, _16, _17, _18, _19, _20, _21, _22,
       _23, _24, _25, _26, _27, _28, _29, _30, _31, _32, and_1_out, and_2_out, n1_bit_set_less_than_1_out_4,
       n1_bit_set_less_than_1_out_5, n1_bit_set_less_than_2_out_4, n1_bit_set_less_than_2_out_5,
       n1_bit_set_less_than_3_out_4, n1_bit_set_less_than_3_out_5, n1_bit_set_less_than_4_out_4,
       n1_bit_set_less_than_4_out_5, n1_bit_set_less_than_5_out_4, n1_bit_set_less_than_5_out_5,
       n1_bit_set_less_than_6_out_4, n1_bit_set_less_than_6_out_5, n1_bit_set_less_than_7_out_4,
       n1_bit_set_less_than_7_out_5, n1_bit_set_less_than_8_out_4, n1_bit_set_less_than_8_out_5,
       n1_bit_set_less_than_9_out_4, n1_bit_set_less_than_9_out_5, n1_bit_set_less_than_10_out_4,
       n1_bit_set_less_than_10_out_5, n1_bit_set_less_than_11_out_4, n1_bit_set_less_than_11_out_5,
       n1_bit_set_less_than_12_out_4, n1_bit_set_less_than_12_out_5, n1_bit_set_less_than_13_out_4,
       n1_bit_set_less_than_13_out_5, n1_bit_set_less_than_14_out_4, n1_bit_set_less_than_14_out_5,
       n1_bit_set_less_than_15_out_4, n1_bit_set_less_than_15_out_5, n1_bit_set_less_than_16_out_4,
       n1_bit_set_less_than_16_out_5, n1_bit_set_less_than_17_out_4, n1_bit_set_less_than_17_out_5,
       n1_bit_set_less_than_18_out_4, n1_bit_set_less_than_18_out_5, n1_bit_set_less_than_19_out_4,
       n1_bit_set_less_than_19_out_5, n1_bit_set_less_than_20_out_4, n1_bit_set_less_than_20_out_5,
       n1_bit_set_less_than_21_out_4, n1_bit_set_less_than_21_out_5, n1_bit_set_less_than_22_out_4,
       n1_bit_set_less_than_22_out_5, n1_bit_set_less_than_23_out_4, n1_bit_set_less_than_23_out_5,
       n1_bit_set_less_than_24_out_4, n1_bit_set_less_than_24_out_5, n1_bit_set_less_than_25_out_4,
       n1_bit_set_less_than_25_out_5, n1_bit_set_less_than_26_out_4, n1_bit_set_less_than_26_out_5,
       n1_bit_set_less_than_27_out_4, n1_bit_set_less_than_27_out_5, n1_bit_set_less_than_28_out_4,
       n1_bit_set_less_than_28_out_5, n1_bit_set_less_than_29_out_4, n1_bit_set_less_than_29_out_5,
       n1_bit_set_less_than_30_out_4, n1_bit_set_less_than_30_out_5, n1_bit_set_less_than_31_out_4,
       n1_bit_set_less_than_31_out_5, n1_bit_set_less_than_32_out_4, n1_bit_set_less_than_32_out_5,
       not_1_out, or_1_out, or_2_out, or_3_out, or_4_out, or_5_out, or_6_out, or_7_out, or_8_out, or_9_out,
       or_10_out, or_11_out, or_12_out, or_13_out, or_14_out, or_15_out, or_16_out, or_17_out, or_18_out,
       or_19_out, or_20_out, or_21_out, or_22_out, or_23_out, or_24_out, or_25_out, or_26_out, or_27_out,
       or_28_out, or_29_out, or_30_out, or_31_out, or_32_out, or_33_out, or_34_out, or_35_out, or_36_out,
       or_37_out, or_38_out, or_39_out, or_40_out, or_41_out, or_42_out, or_43_out, or_44_out, or_45_out,
       or_46_out, or_47_out, or_48_out, or_49_out, or_50_out, or_51_out, or_52_out, or_53_out, or_54_out,
       or_55_out, or_56_out, or_57_out, or_58_out, or_59_out, or_60_out, or_61_out, or_62_out, or_63_out;

  _1_BIT_SET_LESS_THAN u_1_bit_set_less_than_1 (
    .A(A[0]), .B(B[0]), .out_3(_1), .out_4(n1_bit_set_less_than_1_out_4), .out_5(n1_bit_set_less_than_1_out_5));
  _1_BIT_SET_LESS_THAN u_1_bit_set_less_than_2 (
    .A(A[1]), .B(B[1]), .out_3(_2), .out_4(n1_bit_set_less_than_2_out_4), .out_5(n1_bit_set_less_than_2_out_5));
  _1_BIT_SET_LESS_THAN u_1_bit_set_less_than_3 (
    .A(A[2]), .B(B[2]), .out_3(_3), .out_4(n1_bit_set_less_than_3_out_4), .out_5(n1_bit_set_less_than_3_out_5));
  _1_BIT_SET_LESS_THAN u_1_bit_set_less_than_4 (
    .A(A[3]), .B(B[3]), .out_3(_4), .out_4(n1_bit_set_less_than_4_out_4), .out_5(n1_bit_set_less_than_4_out_5));
  _1_BIT_SET_LESS_THAN u_1_bit_set_less_than_5 (
    .A(A[4]), .B(B[4]), .out_3(_5), .out_4(n1_bit_set_less_than_5_out_4), .out_5(n1_bit_set_less_than_5_out_5));
  _1_BIT_SET_LESS_THAN u_1_bit_set_less_than_6 (
    .A(A[5]), .B(B[5]), .out_3(_6), .out_4(n1_bit_set_less_than_6_out_4), .out_5(n1_bit_set_less_than_6_out_5));
  _1_BIT_SET_LESS_THAN u_1_bit_set_less_than_7 (
    .A(A[6]), .B(B[6]), .out_3(_7), .out_4(n1_bit_set_less_than_7_out_4), .out_5(n1_bit_set_less_than_7_out_5));
  _1_BIT_SET_LESS_THAN u_1_bit_set_less_than_8 (
    .A(A[7]), .B(B[7]), .out_3(_8), .out_4(n1_bit_set_less_than_8_out_4), .out_5(n1_bit_set_less_than_8_out_5));
  _1_BIT_SET_LESS_THAN u_1_bit_set_less_than_9 (
    .A(A[8]), .B(B[8]), .out_3(_9), .out_4(n1_bit_set_less_than_9_out_4), .out_5(n1_bit_set_less_than_9_out_5));
  _1_BIT_SET_LESS_THAN u_1_bit_set_less_than_10 (
    .A(A[9]), .B(B[9]), .out_3(_10), .out_4(n1_bit_set_less_than_10_out_4),
    .out_5(n1_bit_set_less_than_10_out_5));
  _1_BIT_SET_LESS_THAN u_1_bit_set_less_than_11 (
    .A(A[10]), .B(B[10]), .out_3(_11), .out_4(n1_bit_set_less_than_11_out_4),
    .out_5(n1_bit_set_less_than_11_out_5));
  _1_BIT_SET_LESS_THAN u_1_bit_set_less_than_12 (
    .A(A[11]), .B(B[11]), .out_3(_12), .out_4(n1_bit_set_less_than_12_out_4),
    .out_5(n1_bit_set_less_than_12_out_5));
  _1_BIT_SET_LESS_THAN u_1_bit_set_less_than_13 (
    .A(A[12]), .B(B[12]), .out_3(_13), .out_4(n1_bit_set_less_than_13_out_4),
    .out_5(n1_bit_set_less_than_13_out_5));
  _1_BIT_SET_LESS_THAN u_1_bit_set_less_than_14 (
    .A(A[13]), .B(B[13]), .out_3(_14), .out_4(n1_bit_set_less_than_14_out_4),
    .out_5(n1_bit_set_less_than_14_out_5));
  _1_BIT_SET_LESS_THAN u_1_bit_set_less_than_15 (
    .A(A[14]), .B(B[14]), .out_3(_15), .out_4(n1_bit_set_less_than_15_out_4),
    .out_5(n1_bit_set_less_than_15_out_5));
  _1_BIT_SET_LESS_THAN u_1_bit_set_less_than_16 (
    .A(A[15]), .B(B[15]), .out_3(_16), .out_4(n1_bit_set_less_than_16_out_4),
    .out_5(n1_bit_set_less_than_16_out_5));
  _1_BIT_SET_LESS_THAN u_1_bit_set_less_than_17 (
    .A(A[16]), .B(B[16]), .out_3(_17), .out_4(n1_bit_set_less_than_17_out_4),
    .out_5(n1_bit_set_less_than_17_out_5));
  _1_BIT_SET_LESS_THAN u_1_bit_set_less_than_18 (
    .A(A[17]), .B(B[17]), .out_3(_18), .out_4(n1_bit_set_less_than_18_out_4),
    .out_5(n1_bit_set_less_than_18_out_5));
  _1_BIT_SET_LESS_THAN u_1_bit_set_less_than_19 (
    .A(A[18]), .B(B[18]), .out_3(_19), .out_4(n1_bit_set_less_than_19_out_4),
    .out_5(n1_bit_set_less_than_19_out_5));
  _1_BIT_SET_LESS_THAN u_1_bit_set_less_than_20 (
    .A(A[19]), .B(B[19]), .out_3(_20), .out_4(n1_bit_set_less_than_20_out_4),
    .out_5(n1_bit_set_less_than_20_out_5));
  _1_BIT_SET_LESS_THAN u_1_bit_set_less_than_21 (
    .A(A[20]), .B(B[20]), .out_3(_21), .out_4(n1_bit_set_less_than_21_out_4),
    .out_5(n1_bit_set_less_than_21_out_5));
  _1_BIT_SET_LESS_THAN u_1_bit_set_less_than_22 (
    .A(A[21]), .B(B[21]), .out_3(_22), .out_4(n1_bit_set_less_than_22_out_4),
    .out_5(n1_bit_set_less_than_22_out_5));
  _1_BIT_SET_LESS_THAN u_1_bit_set_less_than_23 (
    .A(A[22]), .B(B[22]), .out_3(_23), .out_4(n1_bit_set_less_than_23_out_4),
    .out_5(n1_bit_set_less_than_23_out_5));
  _1_BIT_SET_LESS_THAN u_1_bit_set_less_than_24 (
    .A(A[23]), .B(B[23]), .out_3(_24), .out_4(n1_bit_set_less_than_24_out_4),
    .out_5(n1_bit_set_less_than_24_out_5));
  _1_BIT_SET_LESS_THAN u_1_bit_set_less_than_25 (
    .A(A[24]), .B(B[24]), .out_3(_25), .out_4(n1_bit_set_less_than_25_out_4),
    .out_5(n1_bit_set_less_than_25_out_5));
  _1_BIT_SET_LESS_THAN u_1_bit_set_less_than_26 (
    .A(A[25]), .B(B[25]), .out_3(_26), .out_4(n1_bit_set_less_than_26_out_4),
    .out_5(n1_bit_set_less_than_26_out_5));
  _1_BIT_SET_LESS_THAN u_1_bit_set_less_than_27 (
    .A(A[26]), .B(B[26]), .out_3(_27), .out_4(n1_bit_set_less_than_27_out_4),
    .out_5(n1_bit_set_less_than_27_out_5));
  _1_BIT_SET_LESS_THAN u_1_bit_set_less_than_28 (
    .A(A[27]), .B(B[27]), .out_3(_28), .out_4(n1_bit_set_less_than_28_out_4),
    .out_5(n1_bit_set_less_than_28_out_5));
  _1_BIT_SET_LESS_THAN u_1_bit_set_less_than_29 (
    .A(A[28]), .B(B[28]), .out_3(_29), .out_4(n1_bit_set_less_than_29_out_4),
    .out_5(n1_bit_set_less_than_29_out_5));
  _1_BIT_SET_LESS_THAN u_1_bit_set_less_than_30 (
    .A(A[29]), .B(B[29]), .out_3(_30), .out_4(n1_bit_set_less_than_30_out_4),
    .out_5(n1_bit_set_less_than_30_out_5));
  _1_BIT_SET_LESS_THAN u_1_bit_set_less_than_31 (
    .A(A[30]), .B(B[30]), .out_3(_31), .out_4(n1_bit_set_less_than_31_out_4),
    .out_5(n1_bit_set_less_than_31_out_5));
  _1_BIT_SET_LESS_THAN u_1_bit_set_less_than_32 (
    .A(A[31]), .B(B[31]), .out_3(_32), .out_4(n1_bit_set_less_than_32_out_4),
    .out_5(n1_bit_set_less_than_32_out_5));
  or or_1 (or_1_out, _31, _32);
  or or_2 (or_2_out, _29, or_3_out);
  or or_3 (or_3_out, _30, or_1_out);
  or or_4 (or_4_out, n1_bit_set_less_than_31_out_5, n1_bit_set_less_than_32_out_5);
  or or_5 (or_5_out, _28, or_2_out);
  or or_6 (or_6_out, n1_bit_set_less_than_30_out_5, or_4_out);
  or or_7 (or_7_out, _27, or_5_out);
  or or_8 (or_8_out, n1_bit_set_less_than_28_out_5, or_9_out);
  or or_9 (or_9_out, n1_bit_set_less_than_29_out_5, or_6_out);
  or or_10 (or_10_out, _25, or_11_out);
  or or_11 (or_11_out, _26, or_7_out);
  or or_12 (or_12_out, n1_bit_set_less_than_27_out_5, or_8_out);
  or or_13 (or_13_out, _24, or_10_out);
  or or_14 (or_14_out, n1_bit_set_less_than_26_out_5, or_12_out);
  or or_15 (or_15_out, _23, or_13_out);
  or or_16 (or_16_out, n1_bit_set_less_than_24_out_5, or_17_out);
  or or_17 (or_17_out, n1_bit_set_less_than_25_out_5, or_14_out);
  or or_18 (or_18_out, _21, or_19_out);
  or or_19 (or_19_out, _22, or_15_out);
  or or_20 (or_20_out, n1_bit_set_less_than_23_out_5, or_16_out);
  or or_21 (or_21_out, _20, or_18_out);
  or or_22 (or_22_out, n1_bit_set_less_than_22_out_5, or_20_out);
  or or_23 (or_23_out, _19, or_21_out);
  or or_24 (or_24_out, n1_bit_set_less_than_20_out_5, or_25_out);
  or or_25 (or_25_out, n1_bit_set_less_than_21_out_5, or_22_out);
  or or_26 (or_26_out, _17, or_27_out);
  or or_27 (or_27_out, _18, or_23_out);
  or or_28 (or_28_out, n1_bit_set_less_than_19_out_5, or_24_out);
  or or_29 (or_29_out, _16, or_26_out);
  or or_30 (or_30_out, n1_bit_set_less_than_18_out_5, or_28_out);
  or or_31 (or_31_out, _15, or_29_out);
  or or_32 (or_32_out, n1_bit_set_less_than_16_out_5, or_33_out);
  or or_33 (or_33_out, n1_bit_set_less_than_17_out_5, or_30_out);
  or or_34 (or_34_out, _13, or_35_out);
  or or_35 (or_35_out, _14, or_31_out);
  or or_36 (or_36_out, n1_bit_set_less_than_15_out_5, or_32_out);
  or or_37 (or_37_out, _12, or_34_out);
  or or_38 (or_38_out, n1_bit_set_less_than_14_out_5, or_36_out);
  or or_39 (or_39_out, _11, or_37_out);
  or or_40 (or_40_out, n1_bit_set_less_than_12_out_5, or_41_out);
  or or_41 (or_41_out, n1_bit_set_less_than_13_out_5, or_38_out);
  or or_42 (or_42_out, _9, or_43_out);
  or or_43 (or_43_out, _10, or_39_out);
  or or_44 (or_44_out, n1_bit_set_less_than_11_out_5, or_40_out);
  or or_45 (or_45_out, _8, or_42_out);
  or or_46 (or_46_out, n1_bit_set_less_than_10_out_5, or_44_out);
  or or_47 (or_47_out, _7, or_45_out);
  or or_48 (or_48_out, n1_bit_set_less_than_8_out_5, or_49_out);
  or or_49 (or_49_out, n1_bit_set_less_than_9_out_5, or_46_out);
  or or_50 (or_50_out, _5, or_51_out);
  or or_51 (or_51_out, _6, or_47_out);
  or or_52 (or_52_out, n1_bit_set_less_than_7_out_5, or_48_out);
  or or_53 (or_53_out, _4, or_50_out);
  or or_54 (or_54_out, n1_bit_set_less_than_6_out_5, or_52_out);
  or or_55 (or_55_out, _3, or_53_out);
  or or_56 (or_56_out, n1_bit_set_less_than_4_out_5, or_57_out);
  or or_57 (or_57_out, n1_bit_set_less_than_5_out_5, or_54_out);
  or or_58 (or_58_out, _1, or_59_out);
  or or_59 (or_59_out, _2, or_55_out);
  or or_60 (or_60_out, n1_bit_set_less_than_3_out_5, or_56_out);
  or or_61 (or_61_out, n1_bit_set_less_than_2_out_5, or_60_out);
  or or_62 (or_62_out, n1_bit_set_less_than_1_out_5, or_61_out);
  not not_1 (not_1_out, or_62_out);
  or or_63 (or_63_out, and_2_out, or_58_out);
  and and_1 (and_1_out, not_1_out, or_63_out);
  and and_2 (and_2_out, n1_bit_set_less_than_1_out_4, n1_bit_set_less_than_2_out_4, n1_bit_set_less_than_3_out_4, n1_bit_set_less_than_4_out_4, n1_bit_set_less_than_5_out_4, n1_bit_set_less_than_6_out_4, n1_bit_set_less_than_7_out_4, n1_bit_set_less_than_8_out_4, n1_bit_set_less_than_9_out_4, n1_bit_set_less_than_10_out_4, n1_bit_set_less_than_11_out_4, n1_bit_set_less_than_12_out_4, n1_bit_set_less_than_13_out_4, n1_bit_set_less_than_14_out_4, n1_bit_set_less_than_15_out_4, n1_bit_set_less_than_16_out_4, n1_bit_set_less_than_17_out_4, n1_bit_set_less_than_18_out_4, n1_bit_set_less_than_19_out_4, n1_bit_set_less_than_20_out_4, n1_bit_set_less_than_21_out_4, n1_bit_set_less_than_22_out_4, n1_bit_set_less_than_23_out_4, n1_bit_set_less_than_24_out_4, n1_bit_set_less_than_25_out_4, n1_bit_set_less_than_26_out_4, n1_bit_set_less_than_27_out_4, n1_bit_set_less_than_28_out_4, n1_bit_set_less_than_29_out_4, n1_bit_set_less_than_30_out_4, n1_bit_set_less_than_31_out_4, n1_bit_set_less_than_32_out_4);
  not not_2 (out_3[0], and_1_out);

  assign out_3[31:1] = {31{1'b0}};
  // also tied to GND on the sheet: {A[0], A[2], A[3], A[4], A[5], A[6], A[7], A[8], A[9], A[10], A[11], A[12], A[13], A[14], A[15], A[16], A[17], A[18], A[19], A[20], A[21], A[22], A[23], A[24], A[25], A[26], A[27], A[28], A[29], A[30], A[31], B[1], B[2], B[3], B[4], B[5], B[6], B[7], B[8], B[9], B[10], B[11], B[12], B[13], B[14], B[15], B[16], B[17], B[18], B[19], B[20], B[21], B[22], B[23], B[24], B[25], B[26], B[27], B[28], B[29], B[30], B[31]}
  // also tied to VCC on the sheet: {A[1], B[0]}
endmodule
module _32_BIT_SHIFT_RIGHT_ARITHMETIC (
  input  [31:0] A,
  input  [31:0] B,
  output [31:0] Sum
);

  wire multiplexer_1_out, multiplexer_2_out, multiplexer_3_out, multiplexer_4_out, multiplexer_5_out,
       multiplexer_6_out, multiplexer_7_out, multiplexer_8_out, multiplexer_9_out, multiplexer_10_out,
       multiplexer_11_out, multiplexer_12_out, multiplexer_13_out, multiplexer_14_out, multiplexer_15_out,
       multiplexer_16_out, multiplexer_17_out, multiplexer_18_out, multiplexer_19_out, multiplexer_20_out,
       multiplexer_21_out, multiplexer_22_out, multiplexer_23_out, multiplexer_24_out, multiplexer_25_out,
       multiplexer_26_out, multiplexer_27_out, multiplexer_28_out, multiplexer_29_out, multiplexer_30_out,
       multiplexer_31_out, multiplexer_32_out, multiplexer_33_out, multiplexer_34_out, multiplexer_35_out,
       multiplexer_36_out, multiplexer_37_out, multiplexer_38_out, multiplexer_39_out, multiplexer_40_out,
       multiplexer_41_out, multiplexer_42_out, multiplexer_43_out, multiplexer_44_out, multiplexer_45_out,
       multiplexer_46_out, multiplexer_47_out, multiplexer_48_out, multiplexer_49_out, multiplexer_50_out,
       multiplexer_51_out, multiplexer_52_out, multiplexer_53_out, multiplexer_54_out, multiplexer_55_out,
       multiplexer_56_out, multiplexer_57_out, multiplexer_58_out, multiplexer_59_out, multiplexer_60_out,
       multiplexer_61_out, multiplexer_62_out, multiplexer_63_out, multiplexer_64_out, multiplexer_65_out,
       multiplexer_66_out, multiplexer_67_out, multiplexer_68_out, multiplexer_69_out, multiplexer_70_out,
       multiplexer_71_out, multiplexer_72_out, multiplexer_73_out, multiplexer_74_out, multiplexer_75_out,
       multiplexer_76_out, multiplexer_77_out, multiplexer_78_out, multiplexer_79_out, multiplexer_80_out,
       multiplexer_81_out, multiplexer_82_out, multiplexer_83_out, multiplexer_84_out, multiplexer_85_out,
       multiplexer_86_out, multiplexer_87_out, multiplexer_88_out, multiplexer_89_out, multiplexer_90_out,
       multiplexer_91_out, multiplexer_92_out, multiplexer_93_out, multiplexer_94_out, multiplexer_95_out,
       multiplexer_96_out, multiplexer_97_out, multiplexer_98_out, multiplexer_99_out, multiplexer_100_out,
       multiplexer_101_out, multiplexer_102_out, multiplexer_103_out, multiplexer_104_out,
       multiplexer_105_out, multiplexer_106_out, multiplexer_107_out, multiplexer_108_out,
       multiplexer_109_out, multiplexer_110_out, multiplexer_111_out, multiplexer_112_out,
       multiplexer_113_out, multiplexer_114_out, multiplexer_115_out, multiplexer_116_out,
       multiplexer_117_out, multiplexer_118_out, multiplexer_119_out, multiplexer_120_out,
       multiplexer_121_out, multiplexer_122_out, multiplexer_123_out, multiplexer_124_out,
       multiplexer_125_out, multiplexer_126_out, multiplexer_127_out, multiplexer_128_out;

  // Probe on 32'hffff9923
  Multiplexer #(.enable("false")) multiplexer_1 (.in0(A[0]), .in1(A[1]), .out(multiplexer_1_out), .sel(B[0]));
  Multiplexer #(.enable("false")) multiplexer_2 (.in0(A[1]), .in1(A[2]), .out(multiplexer_2_out), .sel(B[0]));
  Multiplexer #(.enable("false")) multiplexer_3 (.in0(A[2]), .in1(A[3]), .out(multiplexer_3_out), .sel(B[0]));
  Multiplexer #(.enable("false")) multiplexer_4 (.in0(A[3]), .in1(A[4]), .out(multiplexer_4_out), .sel(B[0]));
  Multiplexer #(.enable("false")) multiplexer_5 (.in0(A[4]), .in1(A[5]), .out(multiplexer_5_out), .sel(B[0]));
  Multiplexer #(.enable("false")) multiplexer_6 (.in0(A[5]), .in1(A[6]), .out(multiplexer_6_out), .sel(B[0]));
  Multiplexer #(.enable("false")) multiplexer_7 (.in0(A[6]), .in1(A[7]), .out(multiplexer_7_out), .sel(B[0]));
  Multiplexer #(.enable("false")) multiplexer_8 (.in0(A[7]), .in1(A[8]), .out(multiplexer_8_out), .sel(B[0]));
  Multiplexer #(.enable("false")) multiplexer_9 (.in0(A[8]), .in1(A[9]), .out(multiplexer_9_out), .sel(B[0]));
  Multiplexer #(.enable("false")) multiplexer_10 (.in0(A[9]), .in1(A[10]), .out(multiplexer_10_out), .sel(B[0]));
  Multiplexer #(.enable("false")) multiplexer_11 (.in0(A[10]), .in1(A[11]), .out(multiplexer_11_out), .sel(B[0]));
  Multiplexer #(.enable("false")) multiplexer_12 (.in0(A[11]), .in1(A[12]), .out(multiplexer_12_out), .sel(B[0]));
  Multiplexer #(.enable("false")) multiplexer_13 (.in0(A[12]), .in1(A[13]), .out(multiplexer_13_out), .sel(B[0]));
  Multiplexer #(.enable("false")) multiplexer_14 (.in0(A[13]), .in1(A[14]), .out(multiplexer_14_out), .sel(B[0]));
  Multiplexer #(.enable("false")) multiplexer_15 (.in0(A[14]), .in1(A[15]), .out(multiplexer_15_out), .sel(B[0]));
  Multiplexer #(.enable("false")) multiplexer_16 (.in0(A[15]), .in1(A[16]), .out(multiplexer_16_out), .sel(B[0]));
  Multiplexer #(.enable("false")) multiplexer_17 (.in0(A[16]), .in1(A[17]), .out(multiplexer_17_out), .sel(B[0]));
  Multiplexer #(.enable("false")) multiplexer_18 (.in0(A[17]), .in1(A[18]), .out(multiplexer_18_out), .sel(B[0]));
  Multiplexer #(.enable("false")) multiplexer_19 (.in0(A[18]), .in1(A[19]), .out(multiplexer_19_out), .sel(B[0]));
  Multiplexer #(.enable("false")) multiplexer_20 (.in0(A[19]), .in1(A[20]), .out(multiplexer_20_out), .sel(B[0]));
  Multiplexer #(.enable("false")) multiplexer_21 (.in0(A[20]), .in1(A[21]), .out(multiplexer_21_out), .sel(B[0]));
  Multiplexer #(.enable("false")) multiplexer_22 (.in0(A[21]), .in1(A[22]), .out(multiplexer_22_out), .sel(B[0]));
  Multiplexer #(.enable("false")) multiplexer_23 (.in0(A[22]), .in1(A[23]), .out(multiplexer_23_out), .sel(B[0]));
  Multiplexer #(.enable("false")) multiplexer_24 (.in0(A[23]), .in1(A[24]), .out(multiplexer_24_out), .sel(B[0]));
  Multiplexer #(.enable("false")) multiplexer_25 (.in0(A[24]), .in1(A[25]), .out(multiplexer_25_out), .sel(B[0]));
  Multiplexer #(.enable("false")) multiplexer_26 (.in0(A[25]), .in1(A[26]), .out(multiplexer_26_out), .sel(B[0]));
  Multiplexer #(.enable("false")) multiplexer_27 (.in0(A[26]), .in1(A[27]), .out(multiplexer_27_out), .sel(B[0]));
  Multiplexer #(.enable("false")) multiplexer_28 (.in0(A[27]), .in1(A[28]), .out(multiplexer_28_out), .sel(B[0]));
  Multiplexer #(.enable("false")) multiplexer_29 (.in0(A[28]), .in1(A[29]), .out(multiplexer_29_out), .sel(B[0]));
  Multiplexer #(.enable("false")) multiplexer_30 (.in0(A[29]), .in1(A[30]), .out(multiplexer_30_out), .sel(B[0]));
  Multiplexer #(.enable("false")) multiplexer_31 (.in0(A[30]), .in1(A[31]), .out(multiplexer_31_out), .sel(B[0]));
  Multiplexer #(.enable("false")) multiplexer_32 (.in0(A[31]), .in1(A[31]), .out(multiplexer_32_out), .sel(B[0]));
  Multiplexer #(.enable("false")) multiplexer_33 (
    .in0(multiplexer_1_out), .in1(multiplexer_3_out), .out(multiplexer_33_out), .sel(B[1]));
  Multiplexer #(.enable("false")) multiplexer_34 (
    .in0(multiplexer_2_out), .in1(multiplexer_4_out), .out(multiplexer_34_out), .sel(B[1]));
  Multiplexer #(.enable("false")) multiplexer_35 (
    .in0(multiplexer_3_out), .in1(multiplexer_5_out), .out(multiplexer_35_out), .sel(B[1]));
  Multiplexer #(.enable("false")) multiplexer_36 (
    .in0(multiplexer_4_out), .in1(multiplexer_6_out), .out(multiplexer_36_out), .sel(B[1]));
  Multiplexer #(.enable("false")) multiplexer_37 (
    .in0(multiplexer_5_out), .in1(multiplexer_7_out), .out(multiplexer_37_out), .sel(B[1]));
  Multiplexer #(.enable("false")) multiplexer_38 (
    .in0(multiplexer_6_out), .in1(multiplexer_8_out), .out(multiplexer_38_out), .sel(B[1]));
  Multiplexer #(.enable("false")) multiplexer_39 (
    .in0(multiplexer_7_out), .in1(multiplexer_9_out), .out(multiplexer_39_out), .sel(B[1]));
  Multiplexer #(.enable("false")) multiplexer_40 (
    .in0(multiplexer_8_out), .in1(multiplexer_10_out), .out(multiplexer_40_out), .sel(B[1]));
  Multiplexer #(.enable("false")) multiplexer_41 (
    .in0(multiplexer_9_out), .in1(multiplexer_11_out), .out(multiplexer_41_out), .sel(B[1]));
  Multiplexer #(.enable("false")) multiplexer_42 (
    .in0(multiplexer_10_out), .in1(multiplexer_12_out), .out(multiplexer_42_out), .sel(B[1]));
  Multiplexer #(.enable("false")) multiplexer_43 (
    .in0(multiplexer_11_out), .in1(multiplexer_13_out), .out(multiplexer_43_out), .sel(B[1]));
  Multiplexer #(.enable("false")) multiplexer_44 (
    .in0(multiplexer_12_out), .in1(multiplexer_14_out), .out(multiplexer_44_out), .sel(B[1]));
  Multiplexer #(.enable("false")) multiplexer_45 (
    .in0(multiplexer_13_out), .in1(multiplexer_15_out), .out(multiplexer_45_out), .sel(B[1]));
  Multiplexer #(.enable("false")) multiplexer_46 (
    .in0(multiplexer_14_out), .in1(multiplexer_16_out), .out(multiplexer_46_out), .sel(B[1]));
  Multiplexer #(.enable("false")) multiplexer_47 (
    .in0(multiplexer_15_out), .in1(multiplexer_17_out), .out(multiplexer_47_out), .sel(B[1]));
  Multiplexer #(.enable("false")) multiplexer_48 (
    .in0(multiplexer_16_out), .in1(multiplexer_18_out), .out(multiplexer_48_out), .sel(B[1]));
  Multiplexer #(.enable("false")) multiplexer_49 (
    .in0(multiplexer_17_out), .in1(multiplexer_19_out), .out(multiplexer_49_out), .sel(B[1]));
  Multiplexer #(.enable("false")) multiplexer_50 (
    .in0(multiplexer_18_out), .in1(multiplexer_20_out), .out(multiplexer_50_out), .sel(B[1]));
  Multiplexer #(.enable("false")) multiplexer_51 (
    .in0(multiplexer_19_out), .in1(multiplexer_21_out), .out(multiplexer_51_out), .sel(B[1]));
  Multiplexer #(.enable("false")) multiplexer_52 (
    .in0(multiplexer_20_out), .in1(multiplexer_22_out), .out(multiplexer_52_out), .sel(B[1]));
  Multiplexer #(.enable("false")) multiplexer_53 (
    .in0(multiplexer_21_out), .in1(multiplexer_23_out), .out(multiplexer_53_out), .sel(B[1]));
  Multiplexer #(.enable("false")) multiplexer_54 (
    .in0(multiplexer_22_out), .in1(multiplexer_24_out), .out(multiplexer_54_out), .sel(B[1]));
  Multiplexer #(.enable("false")) multiplexer_55 (
    .in0(multiplexer_23_out), .in1(multiplexer_25_out), .out(multiplexer_55_out), .sel(B[1]));
  Multiplexer #(.enable("false")) multiplexer_56 (
    .in0(multiplexer_24_out), .in1(multiplexer_26_out), .out(multiplexer_56_out), .sel(B[1]));
  Multiplexer #(.enable("false")) multiplexer_57 (
    .in0(multiplexer_25_out), .in1(multiplexer_27_out), .out(multiplexer_57_out), .sel(B[1]));
  Multiplexer #(.enable("false")) multiplexer_58 (
    .in0(multiplexer_26_out), .in1(multiplexer_28_out), .out(multiplexer_58_out), .sel(B[1]));
  Multiplexer #(.enable("false")) multiplexer_59 (
    .in0(multiplexer_27_out), .in1(multiplexer_29_out), .out(multiplexer_59_out), .sel(B[1]));
  Multiplexer #(.enable("false")) multiplexer_60 (
    .in0(multiplexer_28_out), .in1(multiplexer_30_out), .out(multiplexer_60_out), .sel(B[1]));
  Multiplexer #(.enable("false")) multiplexer_61 (
    .in0(multiplexer_29_out), .in1(multiplexer_31_out), .out(multiplexer_61_out), .sel(B[1]));
  Multiplexer #(.enable("false")) multiplexer_62 (
    .in0(multiplexer_30_out), .in1(multiplexer_32_out), .out(multiplexer_62_out), .sel(B[1]));
  Multiplexer #(.enable("false")) multiplexer_63 (
    .in0(multiplexer_31_out), .in1(A[31]), .out(multiplexer_63_out), .sel(B[1]));
  Multiplexer #(.enable("false")) multiplexer_64 (
    .in0(multiplexer_32_out), .in1(A[31]), .out(multiplexer_64_out), .sel(B[1]));
  Multiplexer #(.enable("false")) multiplexer_65 (
    .in0(multiplexer_33_out), .in1(multiplexer_37_out), .out(multiplexer_65_out), .sel(B[2]));
  Multiplexer #(.enable("false")) multiplexer_66 (
    .in0(multiplexer_34_out), .in1(multiplexer_38_out), .out(multiplexer_66_out), .sel(B[2]));
  Multiplexer #(.enable("false")) multiplexer_67 (
    .in0(multiplexer_35_out), .in1(multiplexer_39_out), .out(multiplexer_67_out), .sel(B[2]));
  Multiplexer #(.enable("false")) multiplexer_68 (
    .in0(multiplexer_36_out), .in1(multiplexer_40_out), .out(multiplexer_68_out), .sel(B[2]));
  Multiplexer #(.enable("false")) multiplexer_69 (
    .in0(multiplexer_37_out), .in1(multiplexer_41_out), .out(multiplexer_69_out), .sel(B[2]));
  Multiplexer #(.enable("false")) multiplexer_70 (
    .in0(multiplexer_38_out), .in1(multiplexer_42_out), .out(multiplexer_70_out), .sel(B[2]));
  Multiplexer #(.enable("false")) multiplexer_71 (
    .in0(multiplexer_39_out), .in1(multiplexer_43_out), .out(multiplexer_71_out), .sel(B[2]));
  Multiplexer #(.enable("false")) multiplexer_72 (
    .in0(multiplexer_40_out), .in1(multiplexer_44_out), .out(multiplexer_72_out), .sel(B[2]));
  Multiplexer #(.enable("false")) multiplexer_73 (
    .in0(multiplexer_41_out), .in1(multiplexer_45_out), .out(multiplexer_73_out), .sel(B[2]));
  Multiplexer #(.enable("false")) multiplexer_74 (
    .in0(multiplexer_42_out), .in1(multiplexer_46_out), .out(multiplexer_74_out), .sel(B[2]));
  Multiplexer #(.enable("false")) multiplexer_75 (
    .in0(multiplexer_43_out), .in1(multiplexer_47_out), .out(multiplexer_75_out), .sel(B[2]));
  Multiplexer #(.enable("false")) multiplexer_76 (
    .in0(multiplexer_44_out), .in1(multiplexer_48_out), .out(multiplexer_76_out), .sel(B[2]));
  Multiplexer #(.enable("false")) multiplexer_77 (
    .in0(multiplexer_45_out), .in1(multiplexer_49_out), .out(multiplexer_77_out), .sel(B[2]));
  Multiplexer #(.enable("false")) multiplexer_78 (
    .in0(multiplexer_46_out), .in1(multiplexer_50_out), .out(multiplexer_78_out), .sel(B[2]));
  Multiplexer #(.enable("false")) multiplexer_79 (
    .in0(multiplexer_47_out), .in1(multiplexer_51_out), .out(multiplexer_79_out), .sel(B[2]));
  Multiplexer #(.enable("false")) multiplexer_80 (
    .in0(multiplexer_48_out), .in1(multiplexer_52_out), .out(multiplexer_80_out), .sel(B[2]));
  Multiplexer #(.enable("false")) multiplexer_81 (
    .in0(multiplexer_49_out), .in1(multiplexer_53_out), .out(multiplexer_81_out), .sel(B[2]));
  Multiplexer #(.enable("false")) multiplexer_82 (
    .in0(multiplexer_50_out), .in1(multiplexer_54_out), .out(multiplexer_82_out), .sel(B[2]));
  Multiplexer #(.enable("false")) multiplexer_83 (
    .in0(multiplexer_51_out), .in1(multiplexer_55_out), .out(multiplexer_83_out), .sel(B[2]));
  Multiplexer #(.enable("false")) multiplexer_84 (
    .in0(multiplexer_52_out), .in1(multiplexer_56_out), .out(multiplexer_84_out), .sel(B[2]));
  Multiplexer #(.enable("false")) multiplexer_85 (
    .in0(multiplexer_53_out), .in1(multiplexer_57_out), .out(multiplexer_85_out), .sel(B[2]));
  Multiplexer #(.enable("false")) multiplexer_86 (
    .in0(multiplexer_54_out), .in1(multiplexer_58_out), .out(multiplexer_86_out), .sel(B[2]));
  Multiplexer #(.enable("false")) multiplexer_87 (
    .in0(multiplexer_55_out), .in1(multiplexer_59_out), .out(multiplexer_87_out), .sel(B[2]));
  Multiplexer #(.enable("false")) multiplexer_88 (
    .in0(multiplexer_56_out), .in1(multiplexer_60_out), .out(multiplexer_88_out), .sel(B[2]));
  Multiplexer #(.enable("false")) multiplexer_89 (
    .in0(multiplexer_57_out), .in1(multiplexer_61_out), .out(multiplexer_89_out), .sel(B[2]));
  Multiplexer #(.enable("false")) multiplexer_90 (
    .in0(multiplexer_58_out), .in1(multiplexer_62_out), .out(multiplexer_90_out), .sel(B[2]));
  Multiplexer #(.enable("false")) multiplexer_91 (
    .in0(multiplexer_59_out), .in1(multiplexer_63_out), .out(multiplexer_91_out), .sel(B[2]));
  Multiplexer #(.enable("false")) multiplexer_92 (
    .in0(multiplexer_60_out), .in1(multiplexer_64_out), .out(multiplexer_92_out), .sel(B[2]));
  Multiplexer #(.enable("false")) multiplexer_93 (
    .in0(multiplexer_61_out), .in1(A[31]), .out(multiplexer_93_out), .sel(B[2]));
  Multiplexer #(.enable("false")) multiplexer_94 (
    .in0(multiplexer_62_out), .in1(A[31]), .out(multiplexer_94_out), .sel(B[2]));
  Multiplexer #(.enable("false")) multiplexer_95 (
    .in0(multiplexer_63_out), .in1(A[31]), .out(multiplexer_95_out), .sel(B[2]));
  Multiplexer #(.enable("false")) multiplexer_96 (
    .in0(multiplexer_64_out), .in1(A[31]), .out(multiplexer_96_out), .sel(B[2]));
  Multiplexer #(.enable("false")) multiplexer_97 (
    .in0(multiplexer_65_out), .in1(multiplexer_73_out), .out(multiplexer_97_out), .sel(B[3]));
  Multiplexer #(.enable("false")) multiplexer_98 (
    .in0(multiplexer_66_out), .in1(multiplexer_74_out), .out(multiplexer_98_out), .sel(B[3]));
  Multiplexer #(.enable("false")) multiplexer_99 (
    .in0(multiplexer_67_out), .in1(multiplexer_75_out), .out(multiplexer_99_out), .sel(B[3]));
  Multiplexer #(.enable("false")) multiplexer_100 (
    .in0(multiplexer_68_out), .in1(multiplexer_76_out), .out(multiplexer_100_out), .sel(B[3]));
  Multiplexer #(.enable("false")) multiplexer_101 (
    .in0(multiplexer_69_out), .in1(multiplexer_77_out), .out(multiplexer_101_out), .sel(B[3]));
  Multiplexer #(.enable("false")) multiplexer_102 (
    .in0(multiplexer_70_out), .in1(multiplexer_78_out), .out(multiplexer_102_out), .sel(B[3]));
  Multiplexer #(.enable("false")) multiplexer_103 (
    .in0(multiplexer_71_out), .in1(multiplexer_79_out), .out(multiplexer_103_out), .sel(B[3]));
  Multiplexer #(.enable("false")) multiplexer_104 (
    .in0(multiplexer_72_out), .in1(multiplexer_80_out), .out(multiplexer_104_out), .sel(B[3]));
  Multiplexer #(.enable("false")) multiplexer_105 (
    .in0(multiplexer_73_out), .in1(multiplexer_81_out), .out(multiplexer_105_out), .sel(B[3]));
  Multiplexer #(.enable("false")) multiplexer_106 (
    .in0(multiplexer_74_out), .in1(multiplexer_82_out), .out(multiplexer_106_out), .sel(B[3]));
  Multiplexer #(.enable("false")) multiplexer_107 (
    .in0(multiplexer_75_out), .in1(multiplexer_83_out), .out(multiplexer_107_out), .sel(B[3]));
  Multiplexer #(.enable("false")) multiplexer_108 (
    .in0(multiplexer_76_out), .in1(multiplexer_84_out), .out(multiplexer_108_out), .sel(B[3]));
  Multiplexer #(.enable("false")) multiplexer_109 (
    .in0(multiplexer_77_out), .in1(multiplexer_85_out), .out(multiplexer_109_out), .sel(B[3]));
  Multiplexer #(.enable("false")) multiplexer_110 (
    .in0(multiplexer_78_out), .in1(multiplexer_86_out), .out(multiplexer_110_out), .sel(B[3]));
  Multiplexer #(.enable("false")) multiplexer_111 (
    .in0(multiplexer_79_out), .in1(multiplexer_87_out), .out(multiplexer_111_out), .sel(B[3]));
  Multiplexer #(.enable("false")) multiplexer_112 (
    .in0(multiplexer_80_out), .in1(multiplexer_88_out), .out(multiplexer_112_out), .sel(B[3]));
  Multiplexer #(.enable("false")) multiplexer_113 (
    .in0(multiplexer_81_out), .in1(multiplexer_89_out), .out(multiplexer_113_out), .sel(B[3]));
  Multiplexer #(.enable("false")) multiplexer_114 (
    .in0(multiplexer_82_out), .in1(multiplexer_90_out), .out(multiplexer_114_out), .sel(B[3]));
  Multiplexer #(.enable("false")) multiplexer_115 (
    .in0(multiplexer_83_out), .in1(multiplexer_91_out), .out(multiplexer_115_out), .sel(B[3]));
  Multiplexer #(.enable("false")) multiplexer_116 (
    .in0(multiplexer_84_out), .in1(multiplexer_92_out), .out(multiplexer_116_out), .sel(B[3]));
  Multiplexer #(.enable("false")) multiplexer_117 (
    .in0(multiplexer_85_out), .in1(multiplexer_93_out), .out(multiplexer_117_out), .sel(B[3]));
  Multiplexer #(.enable("false")) multiplexer_118 (
    .in0(multiplexer_86_out), .in1(multiplexer_94_out), .out(multiplexer_118_out), .sel(B[3]));
  Multiplexer #(.enable("false")) multiplexer_119 (
    .in0(multiplexer_87_out), .in1(multiplexer_95_out), .out(multiplexer_119_out), .sel(B[3]));
  Multiplexer #(.enable("false")) multiplexer_120 (
    .in0(multiplexer_88_out), .in1(multiplexer_96_out), .out(multiplexer_120_out), .sel(B[3]));
  Multiplexer #(.enable("false")) multiplexer_121 (
    .in0(multiplexer_89_out), .in1(A[31]), .out(multiplexer_121_out), .sel(B[3]));
  Multiplexer #(.enable("false")) multiplexer_122 (
    .in0(multiplexer_90_out), .in1(A[31]), .out(multiplexer_122_out), .sel(B[3]));
  Multiplexer #(.enable("false")) multiplexer_123 (
    .in0(multiplexer_91_out), .in1(A[31]), .out(multiplexer_123_out), .sel(B[3]));
  Multiplexer #(.enable("false")) multiplexer_124 (
    .in0(multiplexer_92_out), .in1(A[31]), .out(multiplexer_124_out), .sel(B[3]));
  Multiplexer #(.enable("false")) multiplexer_125 (
    .in0(multiplexer_93_out), .in1(A[31]), .out(multiplexer_125_out), .sel(B[3]));
  Multiplexer #(.enable("false")) multiplexer_126 (
    .in0(multiplexer_94_out), .in1(A[31]), .out(multiplexer_126_out), .sel(B[3]));
  Multiplexer #(.enable("false")) multiplexer_127 (
    .in0(multiplexer_95_out), .in1(A[31]), .out(multiplexer_127_out), .sel(B[3]));
  Multiplexer #(.enable("false")) multiplexer_128 (
    .in0(multiplexer_96_out), .in1(A[31]), .out(multiplexer_128_out), .sel(B[3]));
  Multiplexer #(.enable("false")) multiplexer_129 (
    .in0(multiplexer_97_out), .in1(multiplexer_113_out), .out(Sum[0]), .sel(B[4]));
  Multiplexer #(.enable("false")) multiplexer_130 (
    .in0(multiplexer_98_out), .in1(multiplexer_114_out), .out(Sum[1]), .sel(B[4]));
  Multiplexer #(.enable("false")) multiplexer_131 (
    .in0(multiplexer_99_out), .in1(multiplexer_115_out), .out(Sum[2]), .sel(B[4]));
  Multiplexer #(.enable("false")) multiplexer_132 (
    .in0(multiplexer_100_out), .in1(multiplexer_116_out), .out(Sum[3]), .sel(B[4]));
  Multiplexer #(.enable("false")) multiplexer_133 (
    .in0(multiplexer_101_out), .in1(multiplexer_117_out), .out(Sum[4]), .sel(B[4]));
  Multiplexer #(.enable("false")) multiplexer_134 (
    .in0(multiplexer_102_out), .in1(multiplexer_118_out), .out(Sum[5]), .sel(B[4]));
  Multiplexer #(.enable("false")) multiplexer_135 (
    .in0(multiplexer_103_out), .in1(multiplexer_119_out), .out(Sum[6]), .sel(B[4]));
  Multiplexer #(.enable("false")) multiplexer_136 (
    .in0(multiplexer_104_out), .in1(multiplexer_120_out), .out(Sum[7]), .sel(B[4]));
  Multiplexer #(.enable("false")) multiplexer_137 (
    .in0(multiplexer_105_out), .in1(multiplexer_121_out), .out(Sum[8]), .sel(B[4]));
  Multiplexer #(.enable("false")) multiplexer_138 (
    .in0(multiplexer_106_out), .in1(multiplexer_122_out), .out(Sum[9]), .sel(B[4]));
  Multiplexer #(.enable("false")) multiplexer_139 (
    .in0(multiplexer_107_out), .in1(multiplexer_123_out), .out(Sum[10]), .sel(B[4]));
  Multiplexer #(.enable("false")) multiplexer_140 (
    .in0(multiplexer_108_out), .in1(multiplexer_124_out), .out(Sum[11]), .sel(B[4]));
  Multiplexer #(.enable("false")) multiplexer_141 (
    .in0(multiplexer_109_out), .in1(multiplexer_125_out), .out(Sum[12]), .sel(B[4]));
  Multiplexer #(.enable("false")) multiplexer_142 (
    .in0(multiplexer_110_out), .in1(multiplexer_126_out), .out(Sum[13]), .sel(B[4]));
  Multiplexer #(.enable("false")) multiplexer_143 (
    .in0(multiplexer_111_out), .in1(multiplexer_127_out), .out(Sum[14]), .sel(B[4]));
  Multiplexer #(.enable("false")) multiplexer_144 (
    .in0(multiplexer_112_out), .in1(multiplexer_128_out), .out(Sum[15]), .sel(B[4]));
  Multiplexer #(.enable("false")) multiplexer_145 (.in0(multiplexer_113_out), .in1(A[31]), .out(Sum[16]), .sel(B[4]));
  Multiplexer #(.enable("false")) multiplexer_146 (.in0(multiplexer_114_out), .in1(A[31]), .out(Sum[17]), .sel(B[4]));
  Multiplexer #(.enable("false")) multiplexer_147 (.in0(multiplexer_115_out), .in1(A[31]), .out(Sum[18]), .sel(B[4]));
  Multiplexer #(.enable("false")) multiplexer_148 (.in0(multiplexer_116_out), .in1(A[31]), .out(Sum[19]), .sel(B[4]));
  Multiplexer #(.enable("false")) multiplexer_149 (.in0(multiplexer_117_out), .in1(A[31]), .out(Sum[20]), .sel(B[4]));
  Multiplexer #(.enable("false")) multiplexer_150 (.in0(multiplexer_118_out), .in1(A[31]), .out(Sum[21]), .sel(B[4]));
  Multiplexer #(.enable("false")) multiplexer_151 (.in0(multiplexer_119_out), .in1(A[31]), .out(Sum[22]), .sel(B[4]));
  Multiplexer #(.enable("false")) multiplexer_152 (.in0(multiplexer_120_out), .in1(A[31]), .out(Sum[23]), .sel(B[4]));
  Multiplexer #(.enable("false")) multiplexer_153 (.in0(multiplexer_121_out), .in1(A[31]), .out(Sum[24]), .sel(B[4]));
  Multiplexer #(.enable("false")) multiplexer_154 (.in0(multiplexer_122_out), .in1(A[31]), .out(Sum[25]), .sel(B[4]));
  Multiplexer #(.enable("false")) multiplexer_155 (.in0(multiplexer_123_out), .in1(A[31]), .out(Sum[26]), .sel(B[4]));
  Multiplexer #(.enable("false")) multiplexer_156 (.in0(multiplexer_124_out), .in1(A[31]), .out(Sum[27]), .sel(B[4]));
  Multiplexer #(.enable("false")) multiplexer_157 (.in0(multiplexer_125_out), .in1(A[31]), .out(Sum[28]), .sel(B[4]));
  Multiplexer #(.enable("false")) multiplexer_158 (.in0(multiplexer_126_out), .in1(A[31]), .out(Sum[29]), .sel(B[4]));
  Multiplexer #(.enable("false")) multiplexer_159 (.in0(multiplexer_127_out), .in1(A[31]), .out(Sum[30]), .sel(B[4]));
  Multiplexer #(.enable("false")) multiplexer_160 (.in0(multiplexer_128_out), .in1(A[31]), .out(Sum[31]), .sel(B[4]));
  // Probe on A
endmodule

module _32_BIT_SHIFT_RIGHT (
  input  [31:0] A,
  input  [31:0] B,
  output [31:0] Sum
);

  wire multiplexer_1_out, multiplexer_2_out, multiplexer_3_out, multiplexer_4_out, multiplexer_5_out,
       multiplexer_6_out, multiplexer_7_out, multiplexer_8_out, multiplexer_9_out, multiplexer_10_out,
       multiplexer_11_out, multiplexer_12_out, multiplexer_13_out, multiplexer_14_out, multiplexer_15_out,
       multiplexer_16_out, multiplexer_17_out, multiplexer_18_out, multiplexer_19_out, multiplexer_20_out,
       multiplexer_21_out, multiplexer_22_out, multiplexer_23_out, multiplexer_24_out, multiplexer_25_out,
       multiplexer_26_out, multiplexer_27_out, multiplexer_28_out, multiplexer_29_out, multiplexer_30_out,
       multiplexer_31_out, multiplexer_32_out, multiplexer_33_out, multiplexer_34_out, multiplexer_35_out,
       multiplexer_36_out, multiplexer_37_out, multiplexer_38_out, multiplexer_39_out, multiplexer_40_out,
       multiplexer_41_out, multiplexer_42_out, multiplexer_43_out, multiplexer_44_out, multiplexer_45_out,
       multiplexer_46_out, multiplexer_47_out, multiplexer_48_out, multiplexer_49_out, multiplexer_50_out,
       multiplexer_51_out, multiplexer_52_out, multiplexer_53_out, multiplexer_54_out, multiplexer_55_out,
       multiplexer_56_out, multiplexer_57_out, multiplexer_58_out, multiplexer_59_out, multiplexer_60_out,
       multiplexer_61_out, multiplexer_62_out, multiplexer_63_out, multiplexer_64_out, multiplexer_65_out,
       multiplexer_66_out, multiplexer_67_out, multiplexer_68_out, multiplexer_69_out, multiplexer_70_out,
       multiplexer_71_out, multiplexer_72_out, multiplexer_73_out, multiplexer_74_out, multiplexer_75_out,
       multiplexer_76_out, multiplexer_77_out, multiplexer_78_out, multiplexer_79_out, multiplexer_80_out,
       multiplexer_81_out, multiplexer_82_out, multiplexer_83_out, multiplexer_84_out, multiplexer_85_out,
       multiplexer_86_out, multiplexer_87_out, multiplexer_88_out, multiplexer_89_out, multiplexer_90_out,
       multiplexer_91_out, multiplexer_92_out, multiplexer_93_out, multiplexer_94_out, multiplexer_95_out,
       multiplexer_96_out, multiplexer_97_out, multiplexer_98_out, multiplexer_99_out, multiplexer_100_out,
       multiplexer_101_out, multiplexer_102_out, multiplexer_103_out, multiplexer_104_out,
       multiplexer_105_out, multiplexer_106_out, multiplexer_107_out, multiplexer_108_out,
       multiplexer_109_out, multiplexer_110_out, multiplexer_111_out, multiplexer_112_out,
       multiplexer_113_out, multiplexer_114_out, multiplexer_115_out, multiplexer_116_out,
       multiplexer_117_out, multiplexer_118_out, multiplexer_119_out, multiplexer_120_out,
       multiplexer_121_out, multiplexer_122_out, multiplexer_123_out, multiplexer_124_out,
       multiplexer_125_out, multiplexer_126_out, multiplexer_127_out, multiplexer_128_out;

  Multiplexer #(.enable("false")) multiplexer_1 (.in0(A[0]), .in1(A[1]), .out(multiplexer_1_out), .sel(B[0]));
  Multiplexer #(.enable("false")) multiplexer_2 (.in0(A[1]), .in1(A[2]), .out(multiplexer_2_out), .sel(B[0]));
  Multiplexer #(.enable("false")) multiplexer_3 (.in0(A[2]), .in1(A[3]), .out(multiplexer_3_out), .sel(B[0]));
  Multiplexer #(.enable("false")) multiplexer_4 (.in0(A[3]), .in1(A[4]), .out(multiplexer_4_out), .sel(B[0]));
  Multiplexer #(.enable("false")) multiplexer_5 (.in0(A[4]), .in1(A[5]), .out(multiplexer_5_out), .sel(B[0]));
  Multiplexer #(.enable("false")) multiplexer_6 (.in0(A[5]), .in1(A[6]), .out(multiplexer_6_out), .sel(B[0]));
  Multiplexer #(.enable("false")) multiplexer_7 (.in0(A[6]), .in1(A[7]), .out(multiplexer_7_out), .sel(B[0]));
  Multiplexer #(.enable("false")) multiplexer_8 (.in0(A[7]), .in1(A[8]), .out(multiplexer_8_out), .sel(B[0]));
  Multiplexer #(.enable("false")) multiplexer_9 (.in0(A[8]), .in1(A[9]), .out(multiplexer_9_out), .sel(B[0]));
  Multiplexer #(.enable("false")) multiplexer_10 (.in0(A[9]), .in1(A[10]), .out(multiplexer_10_out), .sel(B[0]));
  Multiplexer #(.enable("false")) multiplexer_11 (.in0(A[10]), .in1(A[11]), .out(multiplexer_11_out), .sel(B[0]));
  Multiplexer #(.enable("false")) multiplexer_12 (.in0(A[11]), .in1(A[12]), .out(multiplexer_12_out), .sel(B[0]));
  Multiplexer #(.enable("false")) multiplexer_13 (.in0(A[12]), .in1(A[13]), .out(multiplexer_13_out), .sel(B[0]));
  Multiplexer #(.enable("false")) multiplexer_14 (.in0(A[13]), .in1(A[14]), .out(multiplexer_14_out), .sel(B[0]));
  Multiplexer #(.enable("false")) multiplexer_15 (.in0(A[14]), .in1(A[15]), .out(multiplexer_15_out), .sel(B[0]));
  Multiplexer #(.enable("false")) multiplexer_16 (.in0(A[15]), .in1(A[16]), .out(multiplexer_16_out), .sel(B[0]));
  Multiplexer #(.enable("false")) multiplexer_17 (.in0(A[16]), .in1(A[17]), .out(multiplexer_17_out), .sel(B[0]));
  Multiplexer #(.enable("false")) multiplexer_18 (.in0(A[17]), .in1(A[18]), .out(multiplexer_18_out), .sel(B[0]));
  Multiplexer #(.enable("false")) multiplexer_19 (.in0(A[18]), .in1(A[19]), .out(multiplexer_19_out), .sel(B[0]));
  Multiplexer #(.enable("false")) multiplexer_20 (.in0(A[19]), .in1(A[20]), .out(multiplexer_20_out), .sel(B[0]));
  Multiplexer #(.enable("false")) multiplexer_21 (.in0(A[20]), .in1(A[21]), .out(multiplexer_21_out), .sel(B[0]));
  Multiplexer #(.enable("false")) multiplexer_22 (.in0(A[21]), .in1(A[22]), .out(multiplexer_22_out), .sel(B[0]));
  Multiplexer #(.enable("false")) multiplexer_23 (.in0(A[22]), .in1(A[23]), .out(multiplexer_23_out), .sel(B[0]));
  Multiplexer #(.enable("false")) multiplexer_24 (.in0(A[23]), .in1(A[24]), .out(multiplexer_24_out), .sel(B[0]));
  Multiplexer #(.enable("false")) multiplexer_25 (.in0(A[24]), .in1(A[25]), .out(multiplexer_25_out), .sel(B[0]));
  Multiplexer #(.enable("false")) multiplexer_26 (.in0(A[25]), .in1(A[26]), .out(multiplexer_26_out), .sel(B[0]));
  Multiplexer #(.enable("false")) multiplexer_27 (.in0(A[26]), .in1(A[27]), .out(multiplexer_27_out), .sel(B[0]));
  Multiplexer #(.enable("false")) multiplexer_28 (.in0(A[27]), .in1(A[28]), .out(multiplexer_28_out), .sel(B[0]));
  Multiplexer #(.enable("false")) multiplexer_29 (.in0(A[28]), .in1(A[29]), .out(multiplexer_29_out), .sel(B[0]));
  Multiplexer #(.enable("false")) multiplexer_30 (.in0(A[29]), .in1(A[30]), .out(multiplexer_30_out), .sel(B[0]));
  Multiplexer #(.enable("false")) multiplexer_31 (.in0(A[30]), .in1(A[31]), .out(multiplexer_31_out), .sel(B[0]));
  Multiplexer #(.enable("false")) multiplexer_32 (.in0(A[31]), .in1(1'b0), .out(multiplexer_32_out), .sel(B[0]));
  Multiplexer #(.enable("false")) multiplexer_33 (
    .in0(multiplexer_1_out), .in1(multiplexer_3_out), .out(multiplexer_33_out), .sel(B[1]));
  Multiplexer #(.enable("false")) multiplexer_34 (
    .in0(multiplexer_2_out), .in1(multiplexer_4_out), .out(multiplexer_34_out), .sel(B[1]));
  Multiplexer #(.enable("false")) multiplexer_35 (
    .in0(multiplexer_3_out), .in1(multiplexer_5_out), .out(multiplexer_35_out), .sel(B[1]));
  Multiplexer #(.enable("false")) multiplexer_36 (
    .in0(multiplexer_4_out), .in1(multiplexer_6_out), .out(multiplexer_36_out), .sel(B[1]));
  Multiplexer #(.enable("false")) multiplexer_37 (
    .in0(multiplexer_5_out), .in1(multiplexer_7_out), .out(multiplexer_37_out), .sel(B[1]));
  Multiplexer #(.enable("false")) multiplexer_38 (
    .in0(multiplexer_6_out), .in1(multiplexer_8_out), .out(multiplexer_38_out), .sel(B[1]));
  Multiplexer #(.enable("false")) multiplexer_39 (
    .in0(multiplexer_7_out), .in1(multiplexer_9_out), .out(multiplexer_39_out), .sel(B[1]));
  Multiplexer #(.enable("false")) multiplexer_40 (
    .in0(multiplexer_8_out), .in1(multiplexer_10_out), .out(multiplexer_40_out), .sel(B[1]));
  Multiplexer #(.enable("false")) multiplexer_41 (
    .in0(multiplexer_9_out), .in1(multiplexer_11_out), .out(multiplexer_41_out), .sel(B[1]));
  Multiplexer #(.enable("false")) multiplexer_42 (
    .in0(multiplexer_10_out), .in1(multiplexer_12_out), .out(multiplexer_42_out), .sel(B[1]));
  Multiplexer #(.enable("false")) multiplexer_43 (
    .in0(multiplexer_11_out), .in1(multiplexer_13_out), .out(multiplexer_43_out), .sel(B[1]));
  Multiplexer #(.enable("false")) multiplexer_44 (
    .in0(multiplexer_12_out), .in1(multiplexer_14_out), .out(multiplexer_44_out), .sel(B[1]));
  Multiplexer #(.enable("false")) multiplexer_45 (
    .in0(multiplexer_13_out), .in1(multiplexer_15_out), .out(multiplexer_45_out), .sel(B[1]));
  Multiplexer #(.enable("false")) multiplexer_46 (
    .in0(multiplexer_14_out), .in1(multiplexer_16_out), .out(multiplexer_46_out), .sel(B[1]));
  Multiplexer #(.enable("false")) multiplexer_47 (
    .in0(multiplexer_15_out), .in1(multiplexer_17_out), .out(multiplexer_47_out), .sel(B[1]));
  Multiplexer #(.enable("false")) multiplexer_48 (
    .in0(multiplexer_16_out), .in1(multiplexer_18_out), .out(multiplexer_48_out), .sel(B[1]));
  Multiplexer #(.enable("false")) multiplexer_49 (
    .in0(multiplexer_17_out), .in1(multiplexer_19_out), .out(multiplexer_49_out), .sel(B[1]));
  Multiplexer #(.enable("false")) multiplexer_50 (
    .in0(multiplexer_18_out), .in1(multiplexer_20_out), .out(multiplexer_50_out), .sel(B[1]));
  Multiplexer #(.enable("false")) multiplexer_51 (
    .in0(multiplexer_19_out), .in1(multiplexer_21_out), .out(multiplexer_51_out), .sel(B[1]));
  Multiplexer #(.enable("false")) multiplexer_52 (
    .in0(multiplexer_20_out), .in1(multiplexer_22_out), .out(multiplexer_52_out), .sel(B[1]));
  Multiplexer #(.enable("false")) multiplexer_53 (
    .in0(multiplexer_21_out), .in1(multiplexer_23_out), .out(multiplexer_53_out), .sel(B[1]));
  Multiplexer #(.enable("false")) multiplexer_54 (
    .in0(multiplexer_22_out), .in1(multiplexer_24_out), .out(multiplexer_54_out), .sel(B[1]));
  Multiplexer #(.enable("false")) multiplexer_55 (
    .in0(multiplexer_23_out), .in1(multiplexer_25_out), .out(multiplexer_55_out), .sel(B[1]));
  Multiplexer #(.enable("false")) multiplexer_56 (
    .in0(multiplexer_24_out), .in1(multiplexer_26_out), .out(multiplexer_56_out), .sel(B[1]));
  Multiplexer #(.enable("false")) multiplexer_57 (
    .in0(multiplexer_25_out), .in1(multiplexer_27_out), .out(multiplexer_57_out), .sel(B[1]));
  Multiplexer #(.enable("false")) multiplexer_58 (
    .in0(multiplexer_26_out), .in1(multiplexer_28_out), .out(multiplexer_58_out), .sel(B[1]));
  Multiplexer #(.enable("false")) multiplexer_59 (
    .in0(multiplexer_27_out), .in1(multiplexer_29_out), .out(multiplexer_59_out), .sel(B[1]));
  Multiplexer #(.enable("false")) multiplexer_60 (
    .in0(multiplexer_28_out), .in1(multiplexer_30_out), .out(multiplexer_60_out), .sel(B[1]));
  Multiplexer #(.enable("false")) multiplexer_61 (
    .in0(multiplexer_29_out), .in1(multiplexer_31_out), .out(multiplexer_61_out), .sel(B[1]));
  Multiplexer #(.enable("false")) multiplexer_62 (
    .in0(multiplexer_30_out), .in1(multiplexer_32_out), .out(multiplexer_62_out), .sel(B[1]));
  Multiplexer #(.enable("false")) multiplexer_63 (
    .in0(multiplexer_31_out), .in1(1'b0), .out(multiplexer_63_out), .sel(B[1]));
  Multiplexer #(.enable("false")) multiplexer_64 (
    .in0(multiplexer_32_out), .in1(1'b0), .out(multiplexer_64_out), .sel(B[1]));
  Multiplexer #(.enable("false")) multiplexer_65 (
    .in0(multiplexer_33_out), .in1(multiplexer_37_out), .out(multiplexer_65_out), .sel(B[2]));
  Multiplexer #(.enable("false")) multiplexer_66 (
    .in0(multiplexer_34_out), .in1(multiplexer_38_out), .out(multiplexer_66_out), .sel(B[2]));
  Multiplexer #(.enable("false")) multiplexer_67 (
    .in0(multiplexer_35_out), .in1(multiplexer_39_out), .out(multiplexer_67_out), .sel(B[2]));
  Multiplexer #(.enable("false")) multiplexer_68 (
    .in0(multiplexer_36_out), .in1(multiplexer_40_out), .out(multiplexer_68_out), .sel(B[2]));
  Multiplexer #(.enable("false")) multiplexer_69 (
    .in0(multiplexer_37_out), .in1(multiplexer_41_out), .out(multiplexer_69_out), .sel(B[2]));
  Multiplexer #(.enable("false")) multiplexer_70 (
    .in0(multiplexer_38_out), .in1(multiplexer_42_out), .out(multiplexer_70_out), .sel(B[2]));
  Multiplexer #(.enable("false")) multiplexer_71 (
    .in0(multiplexer_39_out), .in1(multiplexer_43_out), .out(multiplexer_71_out), .sel(B[2]));
  Multiplexer #(.enable("false")) multiplexer_72 (
    .in0(multiplexer_40_out), .in1(multiplexer_44_out), .out(multiplexer_72_out), .sel(B[2]));
  Multiplexer #(.enable("false")) multiplexer_73 (
    .in0(multiplexer_41_out), .in1(multiplexer_45_out), .out(multiplexer_73_out), .sel(B[2]));
  Multiplexer #(.enable("false")) multiplexer_74 (
    .in0(multiplexer_42_out), .in1(multiplexer_46_out), .out(multiplexer_74_out), .sel(B[2]));
  Multiplexer #(.enable("false")) multiplexer_75 (
    .in0(multiplexer_43_out), .in1(multiplexer_47_out), .out(multiplexer_75_out), .sel(B[2]));
  Multiplexer #(.enable("false")) multiplexer_76 (
    .in0(multiplexer_44_out), .in1(multiplexer_48_out), .out(multiplexer_76_out), .sel(B[2]));
  Multiplexer #(.enable("false")) multiplexer_77 (
    .in0(multiplexer_45_out), .in1(multiplexer_49_out), .out(multiplexer_77_out), .sel(B[2]));
  Multiplexer #(.enable("false")) multiplexer_78 (
    .in0(multiplexer_46_out), .in1(multiplexer_50_out), .out(multiplexer_78_out), .sel(B[2]));
  Multiplexer #(.enable("false")) multiplexer_79 (
    .in0(multiplexer_47_out), .in1(multiplexer_51_out), .out(multiplexer_79_out), .sel(B[2]));
  Multiplexer #(.enable("false")) multiplexer_80 (
    .in0(multiplexer_48_out), .in1(multiplexer_52_out), .out(multiplexer_80_out), .sel(B[2]));
  Multiplexer #(.enable("false")) multiplexer_81 (
    .in0(multiplexer_49_out), .in1(multiplexer_53_out), .out(multiplexer_81_out), .sel(B[2]));
  Multiplexer #(.enable("false")) multiplexer_82 (
    .in0(multiplexer_50_out), .in1(multiplexer_54_out), .out(multiplexer_82_out), .sel(B[2]));
  Multiplexer #(.enable("false")) multiplexer_83 (
    .in0(multiplexer_51_out), .in1(multiplexer_55_out), .out(multiplexer_83_out), .sel(B[2]));
  Multiplexer #(.enable("false")) multiplexer_84 (
    .in0(multiplexer_52_out), .in1(multiplexer_56_out), .out(multiplexer_84_out), .sel(B[2]));
  Multiplexer #(.enable("false")) multiplexer_85 (
    .in0(multiplexer_53_out), .in1(multiplexer_57_out), .out(multiplexer_85_out), .sel(B[2]));
  Multiplexer #(.enable("false")) multiplexer_86 (
    .in0(multiplexer_54_out), .in1(multiplexer_58_out), .out(multiplexer_86_out), .sel(B[2]));
  Multiplexer #(.enable("false")) multiplexer_87 (
    .in0(multiplexer_55_out), .in1(multiplexer_59_out), .out(multiplexer_87_out), .sel(B[2]));
  Multiplexer #(.enable("false")) multiplexer_88 (
    .in0(multiplexer_56_out), .in1(multiplexer_60_out), .out(multiplexer_88_out), .sel(B[2]));
  Multiplexer #(.enable("false")) multiplexer_89 (
    .in0(multiplexer_57_out), .in1(multiplexer_61_out), .out(multiplexer_89_out), .sel(B[2]));
  Multiplexer #(.enable("false")) multiplexer_90 (
    .in0(multiplexer_58_out), .in1(multiplexer_62_out), .out(multiplexer_90_out), .sel(B[2]));
  Multiplexer #(.enable("false")) multiplexer_91 (
    .in0(multiplexer_59_out), .in1(multiplexer_63_out), .out(multiplexer_91_out), .sel(B[2]));
  Multiplexer #(.enable("false")) multiplexer_92 (
    .in0(multiplexer_60_out), .in1(multiplexer_64_out), .out(multiplexer_92_out), .sel(B[2]));
  Multiplexer #(.enable("false")) multiplexer_93 (
    .in0(multiplexer_61_out), .in1(1'b0), .out(multiplexer_93_out), .sel(B[2]));
  Multiplexer #(.enable("false")) multiplexer_94 (
    .in0(multiplexer_62_out), .in1(1'b0), .out(multiplexer_94_out), .sel(B[2]));
  Multiplexer #(.enable("false")) multiplexer_95 (
    .in0(multiplexer_63_out), .in1(1'b0), .out(multiplexer_95_out), .sel(B[2]));
  Multiplexer #(.enable("false")) multiplexer_96 (
    .in0(multiplexer_64_out), .in1(1'b0), .out(multiplexer_96_out), .sel(B[2]));
  Multiplexer #(.enable("false")) multiplexer_97 (
    .in0(multiplexer_65_out), .in1(multiplexer_73_out), .out(multiplexer_97_out), .sel(B[3]));
  Multiplexer #(.enable("false")) multiplexer_98 (
    .in0(multiplexer_66_out), .in1(multiplexer_74_out), .out(multiplexer_98_out), .sel(B[3]));
  Multiplexer #(.enable("false")) multiplexer_99 (
    .in0(multiplexer_67_out), .in1(multiplexer_75_out), .out(multiplexer_99_out), .sel(B[3]));
  Multiplexer #(.enable("false")) multiplexer_100 (
    .in0(multiplexer_68_out), .in1(multiplexer_76_out), .out(multiplexer_100_out), .sel(B[3]));
  Multiplexer #(.enable("false")) multiplexer_101 (
    .in0(multiplexer_69_out), .in1(multiplexer_77_out), .out(multiplexer_101_out), .sel(B[3]));
  Multiplexer #(.enable("false")) multiplexer_102 (
    .in0(multiplexer_70_out), .in1(multiplexer_78_out), .out(multiplexer_102_out), .sel(B[3]));
  Multiplexer #(.enable("false")) multiplexer_103 (
    .in0(multiplexer_71_out), .in1(multiplexer_79_out), .out(multiplexer_103_out), .sel(B[3]));
  Multiplexer #(.enable("false")) multiplexer_104 (
    .in0(multiplexer_72_out), .in1(multiplexer_80_out), .out(multiplexer_104_out), .sel(B[3]));
  Multiplexer #(.enable("false")) multiplexer_105 (
    .in0(multiplexer_73_out), .in1(multiplexer_81_out), .out(multiplexer_105_out), .sel(B[3]));
  Multiplexer #(.enable("false")) multiplexer_106 (
    .in0(multiplexer_74_out), .in1(multiplexer_82_out), .out(multiplexer_106_out), .sel(B[3]));
  Multiplexer #(.enable("false")) multiplexer_107 (
    .in0(multiplexer_75_out), .in1(multiplexer_83_out), .out(multiplexer_107_out), .sel(B[3]));
  Multiplexer #(.enable("false")) multiplexer_108 (
    .in0(multiplexer_76_out), .in1(multiplexer_84_out), .out(multiplexer_108_out), .sel(B[3]));
  Multiplexer #(.enable("false")) multiplexer_109 (
    .in0(multiplexer_77_out), .in1(multiplexer_85_out), .out(multiplexer_109_out), .sel(B[3]));
  Multiplexer #(.enable("false")) multiplexer_110 (
    .in0(multiplexer_78_out), .in1(multiplexer_86_out), .out(multiplexer_110_out), .sel(B[3]));
  Multiplexer #(.enable("false")) multiplexer_111 (
    .in0(multiplexer_79_out), .in1(multiplexer_87_out), .out(multiplexer_111_out), .sel(B[3]));
  Multiplexer #(.enable("false")) multiplexer_112 (
    .in0(multiplexer_80_out), .in1(multiplexer_88_out), .out(multiplexer_112_out), .sel(B[3]));
  Multiplexer #(.enable("false")) multiplexer_113 (
    .in0(multiplexer_81_out), .in1(multiplexer_89_out), .out(multiplexer_113_out), .sel(B[3]));
  Multiplexer #(.enable("false")) multiplexer_114 (
    .in0(multiplexer_82_out), .in1(multiplexer_90_out), .out(multiplexer_114_out), .sel(B[3]));
  Multiplexer #(.enable("false")) multiplexer_115 (
    .in0(multiplexer_83_out), .in1(multiplexer_91_out), .out(multiplexer_115_out), .sel(B[3]));
  Multiplexer #(.enable("false")) multiplexer_116 (
    .in0(multiplexer_84_out), .in1(multiplexer_92_out), .out(multiplexer_116_out), .sel(B[3]));
  Multiplexer #(.enable("false")) multiplexer_117 (
    .in0(multiplexer_85_out), .in1(multiplexer_93_out), .out(multiplexer_117_out), .sel(B[3]));
  Multiplexer #(.enable("false")) multiplexer_118 (
    .in0(multiplexer_86_out), .in1(multiplexer_94_out), .out(multiplexer_118_out), .sel(B[3]));
  Multiplexer #(.enable("false")) multiplexer_119 (
    .in0(multiplexer_87_out), .in1(multiplexer_95_out), .out(multiplexer_119_out), .sel(B[3]));
  Multiplexer #(.enable("false")) multiplexer_120 (
    .in0(multiplexer_88_out), .in1(multiplexer_96_out), .out(multiplexer_120_out), .sel(B[3]));
  Multiplexer #(.enable("false")) multiplexer_121 (
    .in0(multiplexer_89_out), .in1(1'b0), .out(multiplexer_121_out), .sel(B[3]));
  Multiplexer #(.enable("false")) multiplexer_122 (
    .in0(multiplexer_90_out), .in1(1'b0), .out(multiplexer_122_out), .sel(B[3]));
  Multiplexer #(.enable("false")) multiplexer_123 (
    .in0(multiplexer_91_out), .in1(1'b0), .out(multiplexer_123_out), .sel(B[3]));
  Multiplexer #(.enable("false")) multiplexer_124 (
    .in0(multiplexer_92_out), .in1(1'b0), .out(multiplexer_124_out), .sel(B[3]));
  Multiplexer #(.enable("false")) multiplexer_125 (
    .in0(multiplexer_93_out), .in1(1'b0), .out(multiplexer_125_out), .sel(B[3]));
  Multiplexer #(.enable("false")) multiplexer_126 (
    .in0(multiplexer_94_out), .in1(1'b0), .out(multiplexer_126_out), .sel(B[3]));
  Multiplexer #(.enable("false")) multiplexer_127 (
    .in0(multiplexer_95_out), .in1(1'b0), .out(multiplexer_127_out), .sel(B[3]));
  Multiplexer #(.enable("false")) multiplexer_128 (
    .in0(multiplexer_96_out), .in1(1'b0), .out(multiplexer_128_out), .sel(B[3]));
  Multiplexer #(.enable("false")) multiplexer_129 (
    .in0(multiplexer_97_out), .in1(multiplexer_113_out), .out(Sum[0]), .sel(B[4]));
  Multiplexer #(.enable("false")) multiplexer_130 (
    .in0(multiplexer_98_out), .in1(multiplexer_114_out), .out(Sum[1]), .sel(B[4]));
  Multiplexer #(.enable("false")) multiplexer_131 (
    .in0(multiplexer_99_out), .in1(multiplexer_115_out), .out(Sum[2]), .sel(B[4]));
  Multiplexer #(.enable("false")) multiplexer_132 (
    .in0(multiplexer_100_out), .in1(multiplexer_116_out), .out(Sum[3]), .sel(B[4]));
  Multiplexer #(.enable("false")) multiplexer_133 (
    .in0(multiplexer_101_out), .in1(multiplexer_117_out), .out(Sum[4]), .sel(B[4]));
  Multiplexer #(.enable("false")) multiplexer_134 (
    .in0(multiplexer_102_out), .in1(multiplexer_118_out), .out(Sum[5]), .sel(B[4]));
  Multiplexer #(.enable("false")) multiplexer_135 (
    .in0(multiplexer_103_out), .in1(multiplexer_119_out), .out(Sum[6]), .sel(B[4]));
  Multiplexer #(.enable("false")) multiplexer_136 (
    .in0(multiplexer_104_out), .in1(multiplexer_120_out), .out(Sum[7]), .sel(B[4]));
  Multiplexer #(.enable("false")) multiplexer_137 (
    .in0(multiplexer_105_out), .in1(multiplexer_121_out), .out(Sum[8]), .sel(B[4]));
  Multiplexer #(.enable("false")) multiplexer_138 (
    .in0(multiplexer_106_out), .in1(multiplexer_122_out), .out(Sum[9]), .sel(B[4]));
  Multiplexer #(.enable("false")) multiplexer_139 (
    .in0(multiplexer_107_out), .in1(multiplexer_123_out), .out(Sum[10]), .sel(B[4]));
  Multiplexer #(.enable("false")) multiplexer_140 (
    .in0(multiplexer_108_out), .in1(multiplexer_124_out), .out(Sum[11]), .sel(B[4]));
  Multiplexer #(.enable("false")) multiplexer_141 (
    .in0(multiplexer_109_out), .in1(multiplexer_125_out), .out(Sum[12]), .sel(B[4]));
  Multiplexer #(.enable("false")) multiplexer_142 (
    .in0(multiplexer_110_out), .in1(multiplexer_126_out), .out(Sum[13]), .sel(B[4]));
  Multiplexer #(.enable("false")) multiplexer_143 (
    .in0(multiplexer_111_out), .in1(multiplexer_127_out), .out(Sum[14]), .sel(B[4]));
  Multiplexer #(.enable("false")) multiplexer_144 (
    .in0(multiplexer_112_out), .in1(multiplexer_128_out), .out(Sum[15]), .sel(B[4]));
  Multiplexer #(.enable("false")) multiplexer_145 (.in0(multiplexer_113_out), .in1(1'b0), .out(Sum[16]), .sel(B[4]));
  Multiplexer #(.enable("false")) multiplexer_146 (.in0(multiplexer_114_out), .in1(1'b0), .out(Sum[17]), .sel(B[4]));
  Multiplexer #(.enable("false")) multiplexer_147 (.in0(multiplexer_115_out), .in1(1'b0), .out(Sum[18]), .sel(B[4]));
  Multiplexer #(.enable("false")) multiplexer_148 (.in0(multiplexer_116_out), .in1(1'b0), .out(Sum[19]), .sel(B[4]));
  Multiplexer #(.enable("false")) multiplexer_149 (.in0(multiplexer_117_out), .in1(1'b0), .out(Sum[20]), .sel(B[4]));
  Multiplexer #(.enable("false")) multiplexer_150 (.in0(multiplexer_118_out), .in1(1'b0), .out(Sum[21]), .sel(B[4]));
  Multiplexer #(.enable("false")) multiplexer_151 (.in0(multiplexer_119_out), .in1(1'b0), .out(Sum[22]), .sel(B[4]));
  Multiplexer #(.enable("false")) multiplexer_152 (.in0(multiplexer_120_out), .in1(1'b0), .out(Sum[23]), .sel(B[4]));
  Multiplexer #(.enable("false")) multiplexer_153 (.in0(multiplexer_121_out), .in1(1'b0), .out(Sum[24]), .sel(B[4]));
  Multiplexer #(.enable("false")) multiplexer_154 (.in0(multiplexer_122_out), .in1(1'b0), .out(Sum[25]), .sel(B[4]));
  Multiplexer #(.enable("false")) multiplexer_155 (.in0(multiplexer_123_out), .in1(1'b0), .out(Sum[26]), .sel(B[4]));
  Multiplexer #(.enable("false")) multiplexer_156 (.in0(multiplexer_124_out), .in1(1'b0), .out(Sum[27]), .sel(B[4]));
  Multiplexer #(.enable("false")) multiplexer_157 (.in0(multiplexer_125_out), .in1(1'b0), .out(Sum[28]), .sel(B[4]));
  Multiplexer #(.enable("false")) multiplexer_158 (.in0(multiplexer_126_out), .in1(1'b0), .out(Sum[29]), .sel(B[4]));
  Multiplexer #(.enable("false")) multiplexer_159 (.in0(multiplexer_127_out), .in1(1'b0), .out(Sum[30]), .sel(B[4]));
  Multiplexer #(.enable("false")) multiplexer_160 (.in0(multiplexer_128_out), .in1(1'b0), .out(Sum[31]), .sel(B[4]));
  // Probe on A
endmodule

module _32_BIT_SHIFT_FOR_MULT (
  input  [31:0] in_1,
  input  [31:0] in_2,
  output [31:0] B_OUT,
  output [31:0] A_OUT
);


  assign A_OUT = {in_2[0], in_1[31:1]};
  assign B_OUT = {1'b0, in_2[31:1]};

  // Other names for the same wires on the sheet: A[31:0] = in_1; B[31:0] = in_2
endmodule

module _1_BIT_FULLADDER (
  input  A,
  input  B,
  input  Carry,
  output Sum,
  output Carry_Out
);

  wire and_1_out, and_2_out, xor_1_out;

  xor xor_1 (xor_1_out, A, B);
  xor xor_2 (Sum, xor_1_out, Carry);
  and and_1 (and_1_out, Carry, xor_1_out);
  and and_2 (and_2_out, A, B);
  or or_1 (Carry_Out, and_1_out, and_2_out);

  // Other names for the same wires on the sheet: C = Carry
endmodule

module _1_BIT_SUB (
  input  A,
  input  B,
  input  Carry,
  output difference,
  output Carry_Out
);

  wire and_1_out, and_2_out, not_1_out, not_2_out, xor_1_out;

  not not_1 (not_1_out, A);
  and and_1 (and_1_out, B, not_1_out);
  xor xor_1 (xor_1_out, A, B);
  not not_2 (not_2_out, xor_1_out);
  xor xor_2 (difference, Carry, xor_1_out);
  and and_2 (and_2_out, Carry, not_2_out);
  xor xor_3 (Carry_Out, and_2_out, and_1_out);

  // Other names for the same wires on the sheet: C = Carry
endmodule

module _1_BIT_SET_LESS_THAN (
  input  A,
  input  B,
  output out_3,
  output out_4,
  output out_5
);

  wire not_1_out, not_2_out;

  not not_1 (not_1_out, B);
  not not_2 (not_2_out, A);
  and and_1 (out_3, not_1_out, A);
  and and_2 (out_5, B, not_2_out);
  xnor xnor_1 (out_4, A, B);
endmodule

module depo (
  input  [1:0] B_OUT,
  input  [5:0] B_OUT_2,
  output [5:0] B_OUT_3
);

  wire and_1_out, and_2_out, and_3_out, and_5_out, not_1_out;

  not not_1 (not_1_out, B_OUT_2[3]);
  and and_1 (and_1_out, B_OUT[1], B_OUT_2[3]);
  and and_2 (and_2_out, B_OUT[1], B_OUT_2[1]);
  and and_3 (and_3_out, B_OUT[1], not_1_out, B_OUT_2[0]);
  and and_4 (B_OUT_3[3], B_OUT[1], B_OUT_2[2], B_OUT_2[1]);
  or or_1 (B_OUT_3[2], B_OUT[0], and_1_out);
  and and_5 (and_5_out, B_OUT[1], B_OUT_2[2]);
  or or_2 (B_OUT_3[0], and_2_out, and_3_out);
  not not_2 (B_OUT_3[1], and_5_out);
endmodule

module _32_BIT_NUMBER_COMBINER (
  input  [31:0] B,
  input  [31:0] A,
  output [31:0] O
);


  assign O = {B[30], A[30], B[28], A[28], B[26], A[26], B[24], A[24], B[22], A[22], B[20], A[20], B[18], A[18], B[16], A[16], B[14], A[14], B[12], A[12], B[10], A[10], B[8], A[8], B[6], A[6], B[4], A[4], B[2], A[2], B[0], A[0]};
endmodule

module EQUAL (
  input  [31:0] A,
  input  [31:0] B,
  output [31:0] OUTPUT
);

  wire not_1_out, or_1_out;
  wire [31:0] n32_bit_xor_1__4_bit_out_and;

  _32_BIT_XOR u_32_bit_xor_1 (.A(A), .B(B), ._4_BIT_OUT_AND(n32_bit_xor_1__4_bit_out_and));
  or or_1 (or_1_out, n32_bit_xor_1__4_bit_out_and[0], n32_bit_xor_1__4_bit_out_and[1], n32_bit_xor_1__4_bit_out_and[2], n32_bit_xor_1__4_bit_out_and[3], n32_bit_xor_1__4_bit_out_and[4], n32_bit_xor_1__4_bit_out_and[5], n32_bit_xor_1__4_bit_out_and[6], n32_bit_xor_1__4_bit_out_and[7], n32_bit_xor_1__4_bit_out_and[8], n32_bit_xor_1__4_bit_out_and[9], n32_bit_xor_1__4_bit_out_and[10], n32_bit_xor_1__4_bit_out_and[11], n32_bit_xor_1__4_bit_out_and[12], n32_bit_xor_1__4_bit_out_and[13], n32_bit_xor_1__4_bit_out_and[14], n32_bit_xor_1__4_bit_out_and[15], n32_bit_xor_1__4_bit_out_and[17], n32_bit_xor_1__4_bit_out_and[18], n32_bit_xor_1__4_bit_out_and[19], n32_bit_xor_1__4_bit_out_and[20], n32_bit_xor_1__4_bit_out_and[21], n32_bit_xor_1__4_bit_out_and[22], n32_bit_xor_1__4_bit_out_and[23], n32_bit_xor_1__4_bit_out_and[24], n32_bit_xor_1__4_bit_out_and[25], n32_bit_xor_1__4_bit_out_and[26], n32_bit_xor_1__4_bit_out_and[27], n32_bit_xor_1__4_bit_out_and[28], n32_bit_xor_1__4_bit_out_and[29], n32_bit_xor_1__4_bit_out_and[30], n32_bit_xor_1__4_bit_out_and[31], n32_bit_xor_1__4_bit_out_and[16]);
  not not_1 (not_1_out, or_1_out);
  assign OUTPUT = {{31{1'b0}}, not_1_out};  // Bit_Extender bit_extender_1
endmodule

module NOT_EQUAL (
  input  [31:0] A,
  input  [31:0] B,
  output [31:0] OUTPUT
);

  wire or_1_out;
  wire [31:0] n32_bit_xor_1__4_bit_out_and;

  _32_BIT_XOR u_32_bit_xor_1 (.A(A), .B(B), ._4_BIT_OUT_AND(n32_bit_xor_1__4_bit_out_and));
  or or_1 (or_1_out, n32_bit_xor_1__4_bit_out_and[0], n32_bit_xor_1__4_bit_out_and[1], n32_bit_xor_1__4_bit_out_and[2], n32_bit_xor_1__4_bit_out_and[3], n32_bit_xor_1__4_bit_out_and[4], n32_bit_xor_1__4_bit_out_and[5], n32_bit_xor_1__4_bit_out_and[6], n32_bit_xor_1__4_bit_out_and[7], n32_bit_xor_1__4_bit_out_and[8], n32_bit_xor_1__4_bit_out_and[9], n32_bit_xor_1__4_bit_out_and[10], n32_bit_xor_1__4_bit_out_and[11], n32_bit_xor_1__4_bit_out_and[12], n32_bit_xor_1__4_bit_out_and[13], n32_bit_xor_1__4_bit_out_and[14], n32_bit_xor_1__4_bit_out_and[15], n32_bit_xor_1__4_bit_out_and[17], n32_bit_xor_1__4_bit_out_and[18], n32_bit_xor_1__4_bit_out_and[19], n32_bit_xor_1__4_bit_out_and[20], n32_bit_xor_1__4_bit_out_and[21], n32_bit_xor_1__4_bit_out_and[22], n32_bit_xor_1__4_bit_out_and[23], n32_bit_xor_1__4_bit_out_and[24], n32_bit_xor_1__4_bit_out_and[25], n32_bit_xor_1__4_bit_out_and[26], n32_bit_xor_1__4_bit_out_and[27], n32_bit_xor_1__4_bit_out_and[28], n32_bit_xor_1__4_bit_out_and[29], n32_bit_xor_1__4_bit_out_and[30], n32_bit_xor_1__4_bit_out_and[31], n32_bit_xor_1__4_bit_out_and[16]);
  assign OUTPUT = {{31{1'b0}}, or_1_out};  // Bit_Extender bit_extender_1
endmodule

module beqcontroller (
  input  [31:0] B,
  input  [31:0] A,
  input  [5:0] Controller_IN,
  output OUTPUT,
  output OUTPUT_2
);

  wire beq_2_out, beq_3_out, beq_out, bNq_out, jump_out;
  wire [31:0] equal_1_output, not_equal_1_output;

  and beq (beq_out, ~Controller_IN[0], ~Controller_IN[1], Controller_IN[2], Controller_IN[3], ~Controller_IN[4], ~Controller_IN[5]);  // AND_Gate
  and bNq (bNq_out, Controller_IN[0], ~Controller_IN[1], Controller_IN[2], Controller_IN[3], ~Controller_IN[4], ~Controller_IN[5]);  // AND_Gate
  and jump (jump_out, ~Controller_IN[0], Controller_IN[1], Controller_IN[2], Controller_IN[3], ~Controller_IN[4], ~Controller_IN[5]);  // AND_Gate
  or or_1 (OUTPUT_2, beq_out, bNq_out);
  EQUAL equal_1 (.A(A), .B(B), .OUTPUT(equal_1_output));
  NOT_EQUAL not_equal_1 (.A(A), .B(B), .OUTPUT(not_equal_1_output));
  and beq_2 (beq_2_out, beq_out, equal_1_output[0]);
  and beq_3 (beq_3_out, bNq_out, not_equal_1_output[0]);
  or or_2 (OUTPUT, beq_2_out, beq_3_out, jump_out);

  // Other names for the same wires on the sheet: A_t[31:0] = B; B_t[31:0] = A
endmodule
