// Logisim project 8 Bit Register File.circ as structural Verilog
module _8_Bit_Register_File (
  input  RegWrite,
  input  CLK,
  input  [7:0] Write_Data,
  input  Write_Register,
  input  Read_Register_1,
  input  Read_Register_2,
  output [7:0] Read_Data_1,
  output [7:0] Read_Data_2
);

  wire and_1_out, and_2_out, decoder_1_out0, decoder_1_out1;
  wire [7:0] _0_q, _3_q;

  Decoder #(.enable("false")) decoder_1 (.out0(decoder_1_out0), .out1(decoder_1_out1), .sel(Write_Register));
  and and_1 (and_1_out, decoder_1_out0, RegWrite);
  and and_2 (and_2_out, decoder_1_out1, RegWrite);
  Register _0 (.D(Write_Data), .en(and_1_out), .Q(_0_q), .clk(CLK));  // open: clr
  Register _3 (.D(Write_Data), .en(and_2_out), .Q(_3_q), .clk(CLK));  // open: clr
  Multiplexer #(.width(8), .enable("false")) multiplexer_1 (
    .in0(_0_q), .in1(_3_q), .out(Read_Data_1), .sel(Read_Register_1));
  Multiplexer #(.width(8), .enable("false")) multiplexer_2 (
    .in0(_0_q), .in1(_3_q), .out(Read_Data_2), .sel(Read_Register_2));
endmodule
