// Logisim project Jump.circ as structural Verilog: 2 circuits, main circuit main
module main (
);

  Jump jump_1 ();  // open: PC, Instruction, out_3
endmodule

module Jump (
  input  [7:0] PC,
  input  [7:0] Instruction,
  output [7:0] out_3
);


  assign out_3 = {PC[7:4], Instruction[3:0]};
endmodule
