// Logisim project final design.circ as structural Verilog: 1 circuit, main circuit main
module main (
  output [7:0] out_1,
  output [7:0] out_2,
  output out_3,
  output [1:0] out_4,
  output [3:0] out_5
);

  wire and_1_out, CLK_out, control_unit_1_p2, control_unit_1_p3, control_unit_1_p4, control_unit_1_p5,
       control_unit_1_p6, control_unit_1_p7, control_unit_1_p8, control_unit_1_p9, multiplexer_1_out;
  wire [1:0] control_unit_1_p10;
  wire [2:0] control_unit_1_p1;
  wire [7:0] adder_1_out, adder_2_out, bit_extender_1_out, jump_1_out_3, multiplexer_2_out,
       multiplexer_3_out, multiplexer_4_out, n8_bit_alu_1_alu_output, n8_bit_register_file_1_read_data_1,
       ram_1_data, register_1_q;
  wire [7:3] rom_1_data;

  Register register_1 (.D(multiplexer_4_out), .Q(register_1_q), .clk(CLK_out));  // open: en, clr
  // Control_Unit control_unit_1: pin names not known; wires that end beside it: control_unit_1_p1, control_unit_1_p2, control_unit_1_p3, control_unit_1_p4, control_unit_1_p5, control_unit_1_p6, control_unit_1_p7, control_unit_1_p8, control_unit_1_p9, control_unit_1_p10
  Adder adder_1 (.a(register_1_q), .b({8{1'b0}}), .out(adder_1_out));  // open: cin, cout
  Clock CLK (.out(CLK_out));
  ROM rom_1 (.addr(register_1_q), .data({rom_1_data, control_unit_1_p1}));  // open: sel
  Jump jump_1 (.PC(adder_1_out), .Instruction({rom_1_data, control_unit_1_p1}), .out_3(jump_1_out_3));
  Multiplexer #(.enable("false")) multiplexer_1 (
    .in0(rom_1_data[4]), .in1(rom_1_data[5]), .out(multiplexer_1_out), .sel(control_unit_1_p2));
  _8_Bit_Register_File u_8_bit_register_file_1 (
    .Write_Data(out_2), .Read_Data_1(n8_bit_register_file_1_read_data_1), .Read_Register_1(rom_1_data[3]),
    .Read_Data_2(out_1), .Read_Register_2(rom_1_data[4]), .RegWrite(control_unit_1_p3), .CLK(CLK_out),
    .Write_Register(multiplexer_1_out));
  assign bit_extender_1_out = {{5{1'b0}}, rom_1_data[7:5]};  // Bit_Extender bit_extender_1
  Adder adder_2 (.a(adder_1_out), .b(bit_extender_1_out), .out(adder_2_out));  // open: cin, cout
  Multiplexer #(.width(8), .enable("false")) multiplexer_2 (
    .in0(out_1), .in1(bit_extender_1_out), .out(multiplexer_2_out), .sel(control_unit_1_p4));
  and and_1 (and_1_out, control_unit_1_p8, out_3);
  Multiplexer #(.width(8), .enable("false")) multiplexer_3 (
    .in0(adder_1_out), .in1(adder_2_out), .out(multiplexer_3_out), .sel(and_1_out));
  _8_Bit_ALU u_8_bit_alu_1 (
    .A(n8_bit_register_file_1_read_data_1), .B(multiplexer_2_out), .Zero_Flag(out_3),
    .ALU_Output(n8_bit_alu_1_alu_output), .B_Invert(out_5[2]), .ALU_Op(out_4));  // open: Overflow_Flag, C_Out
  ALU_Control alu_control_1 (
    .ALU_OP(control_unit_1_p10), .Funct_Bits(rom_1_data[7:6]), .ALU_Control_Op({out_5[3:2], out_4}));
  Multiplexer #(.width(8), .enable("false")) multiplexer_4 (
    .in0(multiplexer_3_out), .in1(jump_1_out_3), .out(multiplexer_4_out), .sel(control_unit_1_p9));
  RAM #(.bus("separate")) ram_1 (
    .addr(n8_bit_alu_1_alu_output), .din(out_1), .data(ram_1_data), .str(control_unit_1_p6), .clk(CLK_out),
    .ld(control_unit_1_p5));  // open: sel, clr
  Multiplexer #(.width(8), .enable("false")) multiplexer_5 (
    .in0(n8_bit_alu_1_alu_output), .in1(ram_1_data), .out(out_2), .sel(control_unit_1_p7));

  assign out_5[1:0] = out_4;
endmodule
